// Logisim project Logisim.circ as structural Verilog: 19 circuits, main circuit main
module main (
  input  in_1,
  input  Start_Button,
  input  in_3,
  input  in_4,
  input  in_5,
  input  in_6,
  input  in_7,
  input  in_8,
  input  in_9,
  input  in_10,
  input  Item_1,
  input  Ready_Button,
  input  Item_2,
  input  in_14,
  input  in_15,
  input  Priority,
  input  Priority_2,
  input  in_18,
  input  in_19,
  input  Item_3,
  input  Item_4,
  input  in_22,
  input  in_23,
  input  in_24,
  input  Ready_Button_2,
  input  Priority_3,
  input  in_27,
  input  in_28,
  input  in_29,
  input  in_30,
  input  in_31,
  input  in_32,
  input  in_33,
  input  in_34,
  input  Item_5,
  input  Item_6,
  input  in_37,
  input  Ready_Button_3,
  input  in_39,
  input  in_40,
  input  Priority_4,
  input  in_42,
  input  in_43,
  input  in_44,
  input  in_45,
  input  in_46,
  input  Priority_Service,
  input  in_48,
  output out_49,
  output out_50,
  output out_51,
  output out_52,
  output out_53,
  output out_54,
  output out_55,
  output out_56,
  output out_57,
  output out_58,
  output out_59,
  output out_60,
  output out_61,
  output out_62,
  output out_63,
  output out_64,
  output out_65,
  output out_66,
  output out_67,
  output out_68,
  output out_69,
  output out_70,
  output out_71,
  output out_72,
  output out_73,
  output out_74,
  output out_75,
  output out_76,
  output out_77,
  output out_78,
  output out_79,
  output out_80,
  output out_81,
  output out_82,
  output out_83,
  output out_84,
  output out_85,
  output Priority_Fee,
  output out_87,
  output out_88,
  output out_89,
  output out_90,
  output out_91,
  output out_92,
  output out_93,
  output out_94,
  output out_95,
  output out_96,
  output out_97,
  output out_98,
  output out_99,
  output out_100,
  output out_101,
  output out_102,
  output out_103,
  output out_104,
  output out_105
);

  wire and_11_out, and_12_out, and_13_out, and_14_out, and_15_out, and_16_out, and_17_out, and_18_out,
       and_19_out, and_20_out, and_21_out, and_22_out, and_23_out, and_24_out, and_25_out, and_26_out,
       and_27_out, and_28_out, and_29_out, and_30_out, and_31_out, and_32_out, divide_by_2_1_b0,
       divide_by_2_1_b1, divide_by_2_1_b2, divide_by_2_1_b3, divide_by_2_1_b4, divide_by_2_1_b5,
       divide_by_10_1_b0, divide_by_10_1_b1, divide_by_10_1_b2, divide_by_10_1_b3, half_adder_1_carry,
       half_adder_1_sum, half_adder_2_carry, half_adder_2_sum, half_adder_3_carry, half_adder_3_sum,
       n2_bit_up_counter_1_out_4, n2_bit_up_counter_1_out_5, n3_by_2_multiplier_1_s0,
       n3_by_2_multiplier_1_s1, n3_by_2_multiplier_1_s2, n3_by_2_multiplier_1_s3, n3_by_2_multiplier_2_s0,
       n3_by_2_multiplier_2_s1, n3_by_2_multiplier_2_s2, n3_by_2_multiplier_2_s3, n3_by_2_multiplier_3_s0,
       n3_by_2_multiplier_3_s1, n3_by_2_multiplier_3_s2, n3_by_2_multiplier_3_s3, n4_bit_adder_1_carry,
       n4_bit_adder_1_s0, n4_bit_adder_1_s1, n4_bit_adder_1_s2, n4_bit_adder_1_s3, n4_bit_adder_2_carry,
       n5_bit_adder_1_carry, n5_bit_adder_1_s0, n5_bit_adder_1_s1, n5_bit_adder_1_s2, n5_bit_adder_1_s3,
       n5_bit_adder_1_s4, n5_bit_up_counter_1_lsb, n5_bit_up_counter_1_out_3, n5_bit_up_counter_1_out_4,
       n5_bit_up_counter_1_out_5, n5_bit_up_counter_1_out_6, n5_bit_up_counter_2_lsb,
       n5_bit_up_counter_2_out_3, n5_bit_up_counter_2_out_4, n5_bit_up_counter_2_out_5,
       n5_bit_up_counter_2_out_6, n5_bit_up_counter_3_lsb, n5_bit_up_counter_3_out_3,
       n5_bit_up_counter_3_out_4, n5_bit_up_counter_3_out_5, n5_bit_up_counter_3_out_6,
       n5_by_2_multiplier_1_s0, n5_by_2_multiplier_1_s1, n5_by_2_multiplier_1_s2, n5_by_2_multiplier_1_s3,
       n5_by_2_multiplier_1_s4, n5_by_2_multiplier_1_s5, n5_by_2_multiplier_2_s0, n5_by_2_multiplier_2_s1,
       n5_by_2_multiplier_2_s2, n5_by_2_multiplier_2_s3, n5_by_2_multiplier_2_s4, n5_by_2_multiplier_2_s5,
       n5_by_2_multiplier_3_s0, n5_by_2_multiplier_3_s1, n5_by_2_multiplier_3_s2, n5_by_2_multiplier_3_s3,
       n5_by_2_multiplier_3_s4, n5_by_2_multiplier_3_s5, n6_bit_adder_1_carry, n6_bit_adder_1_s0,
       n6_bit_adder_1_s1, n6_bit_adder_1_s2, n6_bit_adder_1_s3, n6_bit_adder_1_s4, n6_bit_adder_1_s4_2,
       n6_bit_adder_2_carry, n6_bit_adder_3_s0, n6_bit_adder_3_s1, n6_bit_adder_3_s2, n6_bit_adder_3_s3,
       n6_bit_adder_3_s4, n6_bit_adder_3_s4_2, n6_bit_comparator_1_a_b, not_1_out, not_2_out, not_3_out,
       or_3_out, subtract_by_1_1_out_6, subtract_by_1_1_out_7, subtract_by_1_1_out_8, subtract_by_1_2_out_6,
       subtract_by_1_2_out_7, subtract_by_1_2_out_8, subtract_by_1_3_out_6, subtract_by_1_3_out_7,
       subtract_by_1_3_out_8, two_bit_comparator_1_a_b, two_bit_comparator_2_a_b, two_bit_comparator_3_a_b;

  and and_1 (Priority_Fee, Priority_Service, divide_by_10_1_b2);
  and and_2 (out_85, Priority_Service, divide_by_10_1_b3);
  Half_Adder half_adder_1 (.A(Item_3), .B(Item_4), .Sum(half_adder_1_sum), .Carry(half_adder_1_carry));
  _5_by_2_Multiplier u_5_by_2_multiplier_1 (
    .B0(half_adder_2_sum), .B1(half_adder_2_carry), .A4(in_31), .A3(1'b1), .A2(in_32), .A1(1'b1), .A0(in_33),
    .S5(n5_by_2_multiplier_1_s5), .S4(n5_by_2_multiplier_1_s4), .S3(n5_by_2_multiplier_1_s3),
    .S2(n5_by_2_multiplier_1_s2), .S1(n5_by_2_multiplier_1_s1), .S0(n5_by_2_multiplier_1_s0));
  Half_Adder half_adder_2 (.A(Item_5), .B(Item_6), .Sum(half_adder_2_sum), .Carry(half_adder_2_carry));
  Divide_by_10 divide_by_10_1 (
    .A6(out_89), .A5(out_90), .A4(out_91), .A3(out_92), .A2(out_93), .A1(out_94), .A0(out_95),
    .B0(divide_by_10_1_b0), .B1(divide_by_10_1_b1), .B2(divide_by_10_1_b2), .B3(divide_by_10_1_b3));
  and and_3 (out_87, divide_by_10_1_b1, Priority_Service);
  Half_Adder half_adder_3 (.A(Item_1), .B(Item_2), .Sum(half_adder_3_sum), .Carry(half_adder_3_carry));
  _5_by_2_Multiplier u_5_by_2_multiplier_2 (
    .B0(half_adder_1_sum), .B1(half_adder_1_carry), .A4(1'b1), .A3(1'b1), .A2(1'b1), .A1(1'b1), .A0(in_19),
    .S5(n5_by_2_multiplier_2_s5), .S4(n5_by_2_multiplier_2_s4), .S3(n5_by_2_multiplier_2_s3),
    .S2(n5_by_2_multiplier_2_s2), .S1(n5_by_2_multiplier_2_s1), .S0(n5_by_2_multiplier_2_s0));
  and and_4 (out_88, divide_by_10_1_b0, Priority_Service);
  _6_Bit_Adder u_6_bit_adder_1 (
    .B4(n5_by_2_multiplier_2_s5), .A4(n5_by_2_multiplier_3_s5), .B4_2(n5_by_2_multiplier_2_s4),
    .A4_2(n5_by_2_multiplier_3_s4), .B3(n5_by_2_multiplier_2_s3), .A3(n5_by_2_multiplier_3_s3),
    .B2(n5_by_2_multiplier_2_s2), .A2(n5_by_2_multiplier_3_s2), .B1(n5_by_2_multiplier_2_s1),
    .A1(n5_by_2_multiplier_3_s1), .B0(n5_by_2_multiplier_2_s0), .A0(n5_by_2_multiplier_3_s0),
    .Carry(n6_bit_adder_1_carry), .S4(n6_bit_adder_1_s4), .S4_2(n6_bit_adder_1_s4_2), .S3(n6_bit_adder_1_s3),
    .S2(n6_bit_adder_1_s2), .S1(n6_bit_adder_1_s1), .S0(n6_bit_adder_1_s0));
  _6_Bit_Adder u_6_bit_adder_2 (
    .B4(n5_by_2_multiplier_1_s5), .A4(n6_bit_adder_1_s4), .B4_2(n5_by_2_multiplier_1_s4),
    .A4_2(n6_bit_adder_1_s4_2), .B3(n5_by_2_multiplier_1_s3), .A3(n6_bit_adder_1_s3),
    .B2(n5_by_2_multiplier_1_s2), .A2(n6_bit_adder_1_s2), .B1(n5_by_2_multiplier_1_s1),
    .A1(n6_bit_adder_1_s1), .B0(n5_by_2_multiplier_1_s0), .A0(n6_bit_adder_1_s0),
    .Carry(n6_bit_adder_2_carry), .S4(out_90), .S4_2(out_91), .S3(out_92), .S2(out_93), .S1(out_94),
    .S0(out_95));
  or or_1 (out_89, n6_bit_adder_1_carry, n6_bit_adder_2_carry);
  _5_by_2_Multiplier u_5_by_2_multiplier_3 (
    .B0(half_adder_3_sum), .B1(half_adder_3_carry), .A4(1'b1), .A3(in_7), .A2(1'b1), .A1(in_8), .A0(in_9),
    .S5(n5_by_2_multiplier_3_s5), .S4(n5_by_2_multiplier_3_s4), .S3(n5_by_2_multiplier_3_s3),
    .S2(n5_by_2_multiplier_3_s2), .S1(n5_by_2_multiplier_3_s1), .S0(n5_by_2_multiplier_3_s0));
  and and_5 (out_101, divide_by_2_1_b4, and_32_out);
  and and_6 (out_100, divide_by_2_1_b5, and_32_out);
  and and_7 (out_102, divide_by_2_1_b3, and_32_out);
  Subtract_by_1 subtract_by_1_1 (
    .in_4(Priority_Service), .in_5(in_10), .A2(1'b1), .A1(in_4), .A0(1'b1), .out_6(subtract_by_1_1_out_6),
    .out_7(subtract_by_1_1_out_7), .out_8(subtract_by_1_1_out_8));
  _3_by_2_Multiplier u_3_by_2_multiplier_1 (
    .B0(half_adder_3_sum), .B1(half_adder_3_carry), .A2(subtract_by_1_1_out_6), .A1(subtract_by_1_1_out_7),
    .A0(subtract_by_1_1_out_8), .S3(n3_by_2_multiplier_1_s3), .S2(n3_by_2_multiplier_1_s2),
    .S1(n3_by_2_multiplier_1_s1), .S0(n3_by_2_multiplier_1_s0));
  Subtract_by_1 subtract_by_1_2 (
    .in_4(Priority_Service), .in_5(in_22), .A2(1'b1), .A1(1'b1), .A0(1'b1), .out_6(subtract_by_1_2_out_6),
    .out_7(subtract_by_1_2_out_7), .out_8(subtract_by_1_2_out_8));
  _3_by_2_Multiplier u_3_by_2_multiplier_2 (
    .B0(half_adder_1_sum), .B1(half_adder_1_carry), .A2(subtract_by_1_2_out_6), .A1(subtract_by_1_2_out_7),
    .A0(subtract_by_1_2_out_8), .S3(n3_by_2_multiplier_2_s3), .S2(n3_by_2_multiplier_2_s2),
    .S1(n3_by_2_multiplier_2_s1), .S0(n3_by_2_multiplier_2_s0));
  Subtract_by_1 subtract_by_1_3 (
    .in_4(Priority_Service), .in_5(in_37), .A2(in_34), .A1(1'b1), .A0(1'b1), .out_6(subtract_by_1_3_out_6),
    .out_7(subtract_by_1_3_out_7), .out_8(subtract_by_1_3_out_8));
  _3_by_2_Multiplier u_3_by_2_multiplier_3 (
    .B0(half_adder_2_sum), .B1(half_adder_2_carry), .A2(subtract_by_1_3_out_6), .A1(subtract_by_1_3_out_7),
    .A0(subtract_by_1_3_out_8), .S3(n3_by_2_multiplier_3_s3), .S2(n3_by_2_multiplier_3_s2),
    .S1(n3_by_2_multiplier_3_s1), .S0(n3_by_2_multiplier_3_s0));
  Divide_by_2 divide_by_2_1 (
    .A6(out_89), .A5(out_90), .A4(out_91), .A3(out_92), .A2(out_93), .A1(out_94), .A0(out_95),
    .B0(divide_by_2_1_b0), .B1(divide_by_2_1_b1), .B2(divide_by_2_1_b2), .B3(divide_by_2_1_b3),
    .B4(divide_by_2_1_b4), .B5(divide_by_2_1_b5));
  and and_8 (out_103, divide_by_2_1_b2, and_32_out);
  and and_9 (out_104, divide_by_2_1_b1, and_32_out);
  and and_10 (out_105, divide_by_2_1_b0, and_32_out);
  _4_Bit_Adder u_4_bit_adder_1 (
    .B3(n3_by_2_multiplier_2_s3), .A3(n3_by_2_multiplier_1_s3), .B2(n3_by_2_multiplier_2_s2),
    .A2(n3_by_2_multiplier_1_s2), .B1(n3_by_2_multiplier_2_s1), .A1(n3_by_2_multiplier_1_s1),
    .B0(n3_by_2_multiplier_2_s0), .A0(n3_by_2_multiplier_1_s0), .Carry(n4_bit_adder_1_carry),
    .S3(n4_bit_adder_1_s3), .S2(n4_bit_adder_1_s2), .S1(n4_bit_adder_1_s1), .S0(n4_bit_adder_1_s0));
  _4_Bit_Adder u_4_bit_adder_2 (
    .B3(n4_bit_adder_1_s3), .A3(n3_by_2_multiplier_3_s3), .B2(n4_bit_adder_1_s2),
    .A2(n3_by_2_multiplier_3_s2), .B1(n4_bit_adder_1_s1), .A1(n3_by_2_multiplier_3_s1),
    .B0(n4_bit_adder_1_s0), .A0(n3_by_2_multiplier_3_s0), .Carry(n4_bit_adder_2_carry), .S3(out_81),
    .S2(out_82), .S1(out_83), .S0(out_84));
  or or_2 (out_80, n4_bit_adder_1_carry, n4_bit_adder_2_carry);
  _2_bit_Up_Counter u_2_bit_up_counter_1 (
    .Clock(or_3_out), .in_2(1'b1), .in_3(in_3), .out_4(n2_bit_up_counter_1_out_4),
    .out_5(n2_bit_up_counter_1_out_5));
  Two_Bit_Comparator two_bit_comparator_1 (
    .B0(Priority_2), .A0(n2_bit_up_counter_1_out_4), .B1(Priority), .A1(n2_bit_up_counter_1_out_5),
    .A_B(two_bit_comparator_1_a_b));  // open: A_B_2, A_B_3
  and and_11 (and_11_out, n3_by_2_multiplier_1_s3, two_bit_comparator_1_a_b);
  Two_Bit_Comparator two_bit_comparator_2 (
    .B0(in_27), .A0(n2_bit_up_counter_1_out_4), .B1(Priority_3), .A1(n2_bit_up_counter_1_out_5),
    .A_B(two_bit_comparator_2_a_b));  // open: A_B_2, A_B_3
  and and_12 (and_12_out, n3_by_2_multiplier_2_s3, two_bit_comparator_2_a_b);
  Two_Bit_Comparator two_bit_comparator_3 (
    .B0(in_42), .A0(n2_bit_up_counter_1_out_4), .B1(Priority_4), .A1(n2_bit_up_counter_1_out_5),
    .A_B(two_bit_comparator_3_a_b));  // open: A_B_2, A_B_3
  and and_13 (and_13_out, n3_by_2_multiplier_3_s3, two_bit_comparator_3_a_b);
  or or_3 (or_3_out, Start_Button, Ready_Button_3, Ready_Button, Ready_Button_2);
  and and_14 (and_14_out, n3_by_2_multiplier_1_s2, two_bit_comparator_1_a_b);
  and and_15 (and_15_out, n3_by_2_multiplier_2_s2, two_bit_comparator_2_a_b);
  and and_16 (and_16_out, n3_by_2_multiplier_3_s2, two_bit_comparator_3_a_b);
  and and_17 (and_17_out, n3_by_2_multiplier_1_s1, two_bit_comparator_1_a_b);
  and and_18 (and_18_out, n3_by_2_multiplier_1_s0, two_bit_comparator_1_a_b);
  and and_19 (and_19_out, n3_by_2_multiplier_2_s0, two_bit_comparator_2_a_b);
  and and_20 (and_20_out, n3_by_2_multiplier_2_s1, two_bit_comparator_2_a_b, two_bit_comparator_2_a_b);
  and and_21 (and_21_out, n3_by_2_multiplier_3_s1, two_bit_comparator_3_a_b, two_bit_comparator_3_a_b);
  and and_22 (and_22_out, n3_by_2_multiplier_3_s0, two_bit_comparator_3_a_b);
  not not_1 (not_1_out, Ready_Button_2);
  not not_2 (not_2_out, Ready_Button_3);
  or or_4 (out_96, and_13_out, and_12_out, and_11_out);
  _7_Bit_Up_Counter u_7_bit_up_counter_1 (
    .in_1(1'b1), .in_2(in_1), .Clock(Start_Button), .out_4(out_49), .out_5(out_50), .out_6(out_51),
    .out_7(out_52), .out_8(out_53), .out_9(out_54), .out_10(out_55));
  not not_3 (not_3_out, Ready_Button);
  and and_23 (and_23_out, not_1_out, two_bit_comparator_2_a_b);
  and and_24 (and_24_out, not_2_out, two_bit_comparator_3_a_b);
  or or_5 (out_97, and_16_out, and_15_out, and_14_out);
  and and_25 (and_25_out, not_3_out, two_bit_comparator_1_a_b);
  _5_Bit_Up_Counter u_5_bit_up_counter_1 (
    .in_1(and_25_out), .in_2(in_18), .out_3(n5_bit_up_counter_1_out_3), .out_4(n5_bit_up_counter_1_out_4),
    .out_5(n5_bit_up_counter_1_out_5), .out_6(n5_bit_up_counter_1_out_6), .LSB(n5_bit_up_counter_1_lsb));
  _5_Bit_Up_Counter u_5_bit_up_counter_2 (
    .in_1(and_23_out), .in_2(in_30), .out_3(n5_bit_up_counter_2_out_3), .out_4(n5_bit_up_counter_2_out_4),
    .out_5(n5_bit_up_counter_2_out_5), .out_6(n5_bit_up_counter_2_out_6), .LSB(n5_bit_up_counter_2_lsb));
  _5_Bit_Up_Counter u_5_bit_up_counter_3 (
    .in_1(and_24_out), .in_2(in_45), .out_3(n5_bit_up_counter_3_out_3), .out_4(n5_bit_up_counter_3_out_4),
    .out_5(n5_bit_up_counter_3_out_5), .out_6(n5_bit_up_counter_3_out_6), .LSB(n5_bit_up_counter_3_lsb));
  or or_6 (out_98, and_21_out, and_20_out, and_17_out);
  and and_26 (and_26_out, Item_1, Ready_Button);
  and and_27 (and_27_out, Item_2, Ready_Button);
  _4_Bit_Down_Counter u_4_bit_down_counter_1 (
    .in_1(and_26_out), .in_2(1'b1), .in_3(in_5), .in_4(in_6), .out_5(out_56), .out_6(out_57), .out_7(out_58),
    .out_8(out_59));
  _4_Bit_Down_Counter u_4_bit_down_counter_2 (
    .in_1(and_27_out), .in_2(1'b1), .in_3(in_14), .in_4(in_15), .out_5(out_60), .out_6(out_61),
    .out_7(out_62), .out_8(out_63));
  and and_28 (and_28_out, Item_3, Ready_Button_2);
  or or_7 (out_99, and_22_out, and_19_out, and_18_out);
  and and_29 (and_29_out, Item_4, Ready_Button_2);
  and and_30 (and_30_out, Item_5, Ready_Button_3);
  and and_31 (and_31_out, Item_6, Ready_Button_3);
  and and_32 (and_32_out, Priority_Service, n6_bit_comparator_1_a_b);
  _4_Bit_Down_Counter u_4_bit_down_counter_3 (
    .in_1(and_28_out), .in_2(1'b1), .in_3(in_23), .in_4(in_24), .out_5(out_64), .out_6(out_65),
    .out_7(out_66), .out_8(out_67));
  _4_Bit_Down_Counter u_4_bit_down_counter_4 (
    .in_1(and_29_out), .in_2(1'b1), .in_3(in_28), .in_4(in_29), .out_5(out_68), .out_6(out_69),
    .out_7(out_70), .out_8(out_71));
  _4_Bit_Down_Counter u_4_bit_down_counter_5 (
    .in_1(and_30_out), .in_2(1'b1), .in_3(in_39), .in_4(in_40), .out_5(out_72), .out_6(out_73),
    .out_7(out_74), .out_8(out_75));
  _6_Bit_Comparator u_6_bit_comparator_1 (
    .B5(in_48), .A5(n6_bit_adder_3_s4), .B4(out_80), .A4(n6_bit_adder_3_s4_2), .B3(out_81),
    .A3(n6_bit_adder_3_s3), .B2(out_82), .A2(n6_bit_adder_3_s2), .B1(out_83), .A1(n6_bit_adder_3_s1),
    .B0(out_84), .A0(n6_bit_adder_3_s0), .A_B(n6_bit_comparator_1_a_b));
  _4_Bit_Down_Counter u_4_bit_down_counter_6 (
    .in_1(and_31_out), .in_2(1'b1), .in_3(in_43), .in_4(in_44), .out_5(out_76), .out_6(out_77),
    .out_7(out_78), .out_8(out_79));
  _6_Bit_Adder u_6_bit_adder_3 (
    .B4(in_46), .A4(n5_bit_adder_1_carry), .B4_2(n5_bit_up_counter_3_lsb), .A4_2(n5_bit_adder_1_s4),
    .B3(n5_bit_up_counter_3_out_6), .A3(n5_bit_adder_1_s3), .B2(n5_bit_up_counter_3_out_5),
    .A2(n5_bit_adder_1_s2), .B1(n5_bit_up_counter_3_out_4), .A1(n5_bit_adder_1_s1),
    .B0(n5_bit_up_counter_3_out_3), .A0(n5_bit_adder_1_s0), .S4(n6_bit_adder_3_s4),
    .S4_2(n6_bit_adder_3_s4_2), .S3(n6_bit_adder_3_s3), .S2(n6_bit_adder_3_s2), .S1(n6_bit_adder_3_s1),
    .S0(n6_bit_adder_3_s0));  // open: Carry
  _5_Bit_Adder u_5_bit_adder_1 (
    .B4(n5_bit_up_counter_2_lsb), .A4(n5_bit_up_counter_1_lsb), .B3(n5_bit_up_counter_2_out_6),
    .A3(n5_bit_up_counter_1_out_6), .B2(n5_bit_up_counter_2_out_5), .A2(n5_bit_up_counter_1_out_5),
    .B1(n5_bit_up_counter_2_out_4), .A1(n5_bit_up_counter_1_out_4), .B0(n5_bit_up_counter_2_out_3),
    .A0(n5_bit_up_counter_1_out_3), .Carry(n5_bit_adder_1_carry), .S4(n5_bit_adder_1_s4),
    .S3(n5_bit_adder_1_s3), .S2(n5_bit_adder_1_s2), .S1(n5_bit_adder_1_s1), .S0(n5_bit_adder_1_s0));

  // Notes on the sheet:
  //   Starter Section
  //   Main Section
  //   Dessert Section
  //   Cost of each item
  //   Cost of each item
  //   Total Cost of all items ordered 
  //   Cost of each item
  //   Estimated Time of each item
  //   Estimated Time of each item
  //   Estimated Time of each item
  //   Money to be returned
  //   Total Estimated Time to Prepare
  //   Total number of Orders
  //   Estimated Time to Prepare
  //   Available Stock of Item-1 
  //   Available Stock of Item-2
  //   Available Stock of Item-3
  //   Available Stock of Item-4
  //   Available Stock of Item-5
  //   Available Stock of Item-6
  //   Total time taken to serve
  //   Comparing Estimated time with Total time
endmodule

module One_Bit_comparator (
  input  A,
  input  B,
  output E,
  output L,
  output G
);

  wire not_1_out, not_2_out;

  not not_1 (not_1_out, B);
  not not_2 (not_2_out, A);
  xnor xnor_1 (E, A, B);
  and and_1 (L, not_2_out, B);
  and and_2 (G, A, not_1_out);
endmodule

module Two_Bit_Comparator (
  input  B0,
  input  A0,
  input  B1,
  input  A1,
  output A_B,
  output A_B_2,
  output A_B_3
);

  wire and_2_out, and_3_out, one_bit_comparator_1_e, one_bit_comparator_1_g, one_bit_comparator_1_l,
       one_bit_comparator_2_e, one_bit_comparator_2_g, one_bit_comparator_2_l;

  One_Bit_comparator one_bit_comparator_1 (
    .A(A0), .B(B0), .E(one_bit_comparator_1_e), .L(one_bit_comparator_1_l), .G(one_bit_comparator_1_g));
  One_Bit_comparator one_bit_comparator_2 (
    .A(A1), .B(B1), .E(one_bit_comparator_2_e), .L(one_bit_comparator_2_l), .G(one_bit_comparator_2_g));
  and and_1 (A_B, one_bit_comparator_2_e, one_bit_comparator_1_e);
  and and_2 (and_2_out, one_bit_comparator_2_e, one_bit_comparator_1_l);
  and and_3 (and_3_out, one_bit_comparator_2_e, one_bit_comparator_1_g);
  or or_1 (A_B_2, and_2_out, one_bit_comparator_2_l);
  or or_2 (A_B_3, and_3_out, one_bit_comparator_2_g);
endmodule

module _6_Bit_Adder (
  input  B4,
  input  A4,
  input  B4_2,
  input  A4_2,
  input  B3,
  input  A3,
  input  B2,
  input  A2,
  input  B1,
  input  A1,
  input  B0,
  input  A0,
  output Carry,
  output S4,
  output S4_2,
  output S3,
  output S2,
  output S1,
  output S0
);

  wire full_adder_2_carry, full_adder_3_carry, full_adder_4_carry, full_adder_5_carry, half_adder_1_carry;

  Full_Adder full_adder_1 (.A(A4), .B(B4), .C(full_adder_2_carry), .Sum(S4), .Carry(Carry));
  Full_Adder full_adder_2 (.A(A4_2), .B(B4_2), .C(full_adder_3_carry), .Sum(S4_2), .Carry(full_adder_2_carry));
  Full_Adder full_adder_3 (.A(A3), .B(B3), .C(full_adder_4_carry), .Sum(S3), .Carry(full_adder_3_carry));
  Full_Adder full_adder_4 (.A(A2), .B(B2), .C(full_adder_5_carry), .Sum(S2), .Carry(full_adder_4_carry));
  Full_Adder full_adder_5 (.A(A1), .B(B1), .C(half_adder_1_carry), .Sum(S1), .Carry(full_adder_5_carry));
  Half_Adder half_adder_1 (.A(A0), .B(B0), .Sum(S0), .Carry(half_adder_1_carry));
endmodule

module Full_Adder (
  input  A,
  input  B,
  input  C,
  output Sum,
  output Carry
);

  wire and_1_out, and_2_out, xor_1_out;

  xor xor_1 (xor_1_out, A, B);
  and and_1 (and_1_out, A, B);
  xor xor_2 (Sum, xor_1_out, C);
  and and_2 (and_2_out, xor_1_out, C);
  or or_1 (Carry, and_2_out, and_1_out);
endmodule

module _4_Bit_Down_Counter (
  input  in_1,
  input  in_2,
  input  in_3,
  input  in_4,
  output out_5,
  output out_6,
  output out_7,
  output out_8
);

  wire j_k_ff_1_qn, j_k_ff_2_qn, j_k_ff_3_qn;

  J_K_Flip_Flop #(.trigger("falling")) j_k_ff_1 (
    .J(in_2), .clk(in_1), .K(in_2), .Q(out_8), .Qn(j_k_ff_1_qn), .preset(in_4), .reset(in_3));  // open: en
  J_K_Flip_Flop #(.trigger("falling")) j_k_ff_2 (
    .J(in_2), .clk(j_k_ff_1_qn), .K(in_2), .Q(out_7), .Qn(j_k_ff_2_qn), .preset(in_4), .reset(in_3));  // open: en
  J_K_Flip_Flop #(.trigger("falling")) j_k_ff_3 (
    .J(in_2), .clk(j_k_ff_2_qn), .K(in_2), .Q(out_6), .Qn(j_k_ff_3_qn), .preset(in_4), .reset(in_3));  // open: en
  J_K_Flip_Flop #(.trigger("falling")) j_k_ff_4 (
    .J(in_2), .clk(j_k_ff_3_qn), .K(in_2), .Q(out_5), .preset(in_4), .reset(in_3));  // open: Qn, en
endmodule

module _5_Bit_Up_Counter (
  input  in_1,
  input  in_2,
  output out_3,
  output out_4,
  output out_5,
  output out_6,
  output LSB
);

  wire clock_1_out, j_k_ff_1_qn, j_k_ff_2_qn, j_k_ff_3_qn, j_k_ff_4_qn;

  Clock clock_1 (.out(clock_1_out));
  J_K_Flip_Flop j_k_ff_1 (
    .J(in_1), .clk(clock_1_out), .K(in_1), .Q(LSB), .Qn(j_k_ff_1_qn), .preset(in_2), .reset(in_2));  // open: en
  J_K_Flip_Flop j_k_ff_2 (
    .J(in_1), .clk(j_k_ff_1_qn), .K(in_1), .Q(out_6), .Qn(j_k_ff_2_qn), .preset(in_2), .reset(in_2));  // open: en
  J_K_Flip_Flop j_k_ff_3 (
    .J(in_1), .clk(j_k_ff_2_qn), .K(in_1), .Q(out_5), .Qn(j_k_ff_3_qn), .preset(in_2), .reset(in_2));  // open: en
  J_K_Flip_Flop j_k_ff_4 (
    .J(in_1), .clk(j_k_ff_3_qn), .K(in_1), .Q(out_4), .Qn(j_k_ff_4_qn), .preset(in_2), .reset(in_2));  // open: en
  J_K_Flip_Flop j_k_ff_5 (
    .J(in_1), .clk(j_k_ff_4_qn), .K(in_1), .Q(out_3), .preset(in_2), .reset(in_2));  // open: Qn, en
endmodule

module Half_Adder (
  input  A,
  input  B,
  output Sum,
  output Carry
);

  xor xor_1 (Sum, A, B);
  and and_1 (Carry, B, A);
endmodule

module _5_by_2_Multiplier (
  input  A4,
  input  A3,
  input  A2,
  input  A1,
  input  A0,
  input  B0,
  input  B1,
  output S5,
  output S4,
  output S3,
  output S2,
  output S1,
  output S0
);

  wire and_1_out, and_2_out, and_3_out, and_4_out, and_5_out, and_6_out, and_7_out, and_8_out, and_9_out,
       full_adder_1_carry, full_adder_2_carry, full_adder_3_carry, half_adder_2_carry;

  and and_1 (and_1_out, B0, A4);
  and and_2 (and_2_out, B1, A4);
  Half_Adder half_adder_1 (.A(full_adder_1_carry), .B(and_2_out), .Sum(S5));  // open: Carry
  and and_3 (and_3_out, B0, A3);
  and and_4 (and_4_out, B1, A3);
  Full_Adder full_adder_1 (.A(full_adder_2_carry), .B(and_4_out), .C(and_1_out), .Sum(S4), .Carry(full_adder_1_carry));
  Full_Adder full_adder_2 (.A(full_adder_3_carry), .B(and_6_out), .C(and_3_out), .Sum(S3), .Carry(full_adder_2_carry));
  and and_5 (and_5_out, B0, A2);
  and and_6 (and_6_out, B1, A2);
  Full_Adder full_adder_3 (.A(half_adder_2_carry), .B(and_9_out), .C(and_5_out), .Sum(S2), .Carry(full_adder_3_carry));
  and and_7 (and_7_out, B0, A1);
  and and_8 (and_8_out, B1, A0);
  and and_9 (and_9_out, B1, A1);
  Half_Adder half_adder_2 (.A(and_8_out), .B(and_7_out), .Sum(S1), .Carry(half_adder_2_carry));
  and and_10 (S0, B0, A0);
endmodule

module _2_bit_Up_Counter (
  input  Clock,
  input  in_2,
  input  in_3,
  output out_4,
  output out_5
);

  wire j_k_ff_1_qn;

  J_K_Flip_Flop #(.trigger("falling")) j_k_ff_1 (
    .J(in_2), .clk(Clock), .K(in_2), .Q(out_5), .Qn(j_k_ff_1_qn), .preset(in_3), .reset(in_3));  // open: en
  J_K_Flip_Flop j_k_ff_2 (
    .J(in_2), .clk(j_k_ff_1_qn), .K(in_2), .Q(out_4), .preset(in_3), .reset(in_3));  // open: Qn, en
endmodule

module _3_by_2_Multiplier (
  input  A2,
  input  A1,
  input  A0,
  input  B0,
  input  B1,
  output S3,
  output S2,
  output S1,
  output S0
);

  wire and_1_out, and_2_out, and_3_out, and_4_out, and_5_out, full_adder_1_carry, half_adder_2_carry;

  Half_Adder half_adder_1 (.A(full_adder_1_carry), .B(and_2_out), .Sum(S3));  // open: Carry
  and and_1 (and_1_out, B0, A2);
  and and_2 (and_2_out, B1, A2);
  Full_Adder full_adder_1 (.A(half_adder_2_carry), .B(and_4_out), .C(and_1_out), .Sum(S2), .Carry(full_adder_1_carry));
  and and_3 (and_3_out, B0, A1);
  and and_4 (and_4_out, B1, A1);
  and and_5 (and_5_out, B1, A0);
  Half_Adder half_adder_2 (.A(and_5_out), .B(and_3_out), .Sum(S1), .Carry(half_adder_2_carry));
  and and_6 (S0, B0, A0);
endmodule

module _7_Bit_Up_Counter (
  input  in_1,
  input  in_2,
  input  Clock,
  output out_4,
  output out_5,
  output out_6,
  output out_7,
  output out_8,
  output out_9,
  output out_10
);

  wire j_k_ff_2_qn, j_k_ff_3_qn, j_k_ff_4_qn, j_k_ff_5_qn, j_k_ff_6_qn, j_k_ff_7_qn;

  J_K_Flip_Flop j_k_ff_1 (
    .J(in_1), .clk(j_k_ff_2_qn), .K(in_1), .Q(out_4), .preset(in_2), .reset(in_2));  // open: Qn, en
  J_K_Flip_Flop j_k_ff_2 (
    .J(in_1), .clk(j_k_ff_3_qn), .K(in_1), .Q(out_5), .Qn(j_k_ff_2_qn), .preset(in_2), .reset(in_2));  // open: en
  J_K_Flip_Flop j_k_ff_3 (
    .J(in_1), .clk(j_k_ff_4_qn), .K(in_1), .Q(out_6), .Qn(j_k_ff_3_qn), .preset(in_2), .reset(in_2));  // open: en
  J_K_Flip_Flop j_k_ff_4 (
    .J(in_1), .clk(j_k_ff_5_qn), .K(in_1), .Q(out_7), .Qn(j_k_ff_4_qn), .preset(in_2), .reset(in_2));  // open: en
  J_K_Flip_Flop j_k_ff_5 (
    .J(in_1), .clk(j_k_ff_6_qn), .K(in_1), .Q(out_8), .Qn(j_k_ff_5_qn), .preset(in_2), .reset(in_2));  // open: en
  J_K_Flip_Flop j_k_ff_6 (
    .J(in_1), .clk(j_k_ff_7_qn), .K(in_1), .Q(out_9), .Qn(j_k_ff_6_qn), .preset(in_2), .reset(in_2));  // open: en
  J_K_Flip_Flop #(.trigger("falling")) j_k_ff_7 (
    .J(in_1), .clk(Clock), .K(in_1), .Q(out_10), .Qn(j_k_ff_7_qn), .preset(in_2), .reset(in_2));  // open: en
endmodule

module Divide_by_2 (
  input  A6,
  input  A5,
  input  A4,
  input  A3,
  input  A2,
  input  A1,
  input  A0,
  output B0,
  output B1,
  output B2,
  output B3,
  output B4,
  output B5
);


  assign B0 = A1;
  assign B1 = A2;
  assign B2 = A3;
  assign B3 = A4;
  assign B4 = A5;
  assign B5 = A6;
endmodule

module Divide_by_10 (
  input  A6,
  input  A5,
  input  A4,
  input  A3,
  input  A2,
  input  A1,
  input  A0,
  output B0,
  output B1,
  output B2,
  output B3
);


  assign B0 = A3;
  assign B1 = A4;
  assign B2 = A5;
  assign B3 = A6;

  // Notes on the sheet:
  //   This is the logisim part for the 10% of the cost.
endmodule

module Full_Subtractor (
  input  A,
  input  B,
  input  C,
  output Difference,
  output Borrow
);

  wire and_1_out, and_2_out, not_1_out, not_2_out, xor_1_out;

  xor xor_1 (xor_1_out, A, B);
  xor xor_2 (Difference, xor_1_out, C);
  not not_1 (not_1_out, xor_1_out);
  not not_2 (not_2_out, A);
  and and_1 (and_1_out, not_1_out, C);
  and and_2 (and_2_out, not_2_out, B);
  or or_1 (Borrow, and_1_out, and_2_out);
endmodule

module Subtract_by_1 (
  input  A2,
  input  A1,
  input  A0,
  input  in_4,
  input  in_5,
  output out_6,
  output out_7,
  output out_8
);

  wire full_subtractor_2_borrow, full_subtractor_3_borrow;

  Full_Subtractor full_subtractor_1 (
    .A(A2), .B(in_5), .C(full_subtractor_2_borrow), .Difference(out_6));  // open: Borrow
  Full_Subtractor full_subtractor_2 (
    .A(A1), .B(in_5), .C(full_subtractor_3_borrow), .Difference(out_7), .Borrow(full_subtractor_2_borrow));
  Full_Subtractor full_subtractor_3 (.A(A0), .B(in_4), .C(in_5), .Difference(out_8), .Borrow(full_subtractor_3_borrow));
endmodule

module _4_Bit_Adder (
  input  B3,
  input  A3,
  input  B2,
  input  A2,
  input  B1,
  input  A1,
  input  B0,
  input  A0,
  output Carry,
  output S3,
  output S2,
  output S1,
  output S0
);

  wire full_adder_2_carry, full_adder_3_carry, half_adder_1_carry;

  Full_Adder full_adder_1 (.A(A3), .B(B3), .C(full_adder_2_carry), .Sum(S3), .Carry(Carry));
  Full_Adder full_adder_2 (.A(A2), .B(B2), .C(full_adder_3_carry), .Sum(S2), .Carry(full_adder_2_carry));
  Full_Adder full_adder_3 (.A(A1), .B(B1), .C(half_adder_1_carry), .Sum(S1), .Carry(full_adder_3_carry));
  Half_Adder half_adder_1 (.A(A0), .B(B0), .Sum(S0), .Carry(half_adder_1_carry));
endmodule

module _5_Bit_Adder (
  input  B4,
  input  A4,
  input  B3,
  input  A3,
  input  B2,
  input  A2,
  input  B1,
  input  A1,
  input  B0,
  input  A0,
  output Carry,
  output S4,
  output S3,
  output S2,
  output S1,
  output S0
);

  wire full_adder_2_carry, full_adder_3_carry, full_adder_4_carry, half_adder_1_carry;

  Full_Adder full_adder_1 (.A(A4), .B(B4), .C(full_adder_2_carry), .Sum(S4), .Carry(Carry));
  Full_Adder full_adder_2 (.A(A3), .B(B3), .C(full_adder_3_carry), .Sum(S3), .Carry(full_adder_2_carry));
  Full_Adder full_adder_3 (.A(A2), .B(B2), .C(full_adder_4_carry), .Sum(S2), .Carry(full_adder_3_carry));
  Full_Adder full_adder_4 (.A(A1), .B(B1), .C(half_adder_1_carry), .Sum(S1), .Carry(full_adder_4_carry));
  Half_Adder half_adder_1 (.A(A0), .B(B0), .Sum(S0), .Carry(half_adder_1_carry));
endmodule

module _6_Bit_Comparator (
  input  B5,
  input  A5,
  input  B4,
  input  A4,
  input  B3,
  input  A3,
  input  B2,
  input  A2,
  input  B1,
  input  A1,
  input  B0,
  input  A0,
  output A_B
);

  wire and_1_out, and_2_out, and_3_out, and_4_out, and_5_out, one_bit_comparator_1_e, one_bit_comparator_1_g,
       one_bit_comparator_2_e, one_bit_comparator_2_g, one_bit_comparator_3_e, one_bit_comparator_3_g,
       one_bit_comparator_4_e, one_bit_comparator_4_g, one_bit_comparator_5_e, one_bit_comparator_5_g,
       one_bit_comparator_6_g;

  One_Bit_comparator one_bit_comparator_1 (
    .A(A5), .B(B5), .E(one_bit_comparator_1_e), .G(one_bit_comparator_1_g));  // open: L
  One_Bit_comparator one_bit_comparator_2 (
    .A(A4), .B(B4), .E(one_bit_comparator_2_e), .G(one_bit_comparator_2_g));  // open: L
  One_Bit_comparator one_bit_comparator_3 (
    .A(A3), .B(B3), .E(one_bit_comparator_3_e), .G(one_bit_comparator_3_g));  // open: L
  One_Bit_comparator one_bit_comparator_4 (
    .A(A2), .B(B2), .E(one_bit_comparator_4_e), .G(one_bit_comparator_4_g));  // open: L
  One_Bit_comparator one_bit_comparator_5 (
    .A(A1), .B(B1), .E(one_bit_comparator_5_e), .G(one_bit_comparator_5_g));  // open: L
  One_Bit_comparator one_bit_comparator_6 (.A(A0), .B(B0), .G(one_bit_comparator_6_g));  // open: E, L
  and and_1 (and_1_out, one_bit_comparator_1_e, one_bit_comparator_2_g);
  and and_2 (and_2_out, one_bit_comparator_1_e, one_bit_comparator_2_e, one_bit_comparator_3_g);
  and and_3 (and_3_out, one_bit_comparator_1_e, one_bit_comparator_2_e, one_bit_comparator_3_e, one_bit_comparator_4_g);
  and and_4 (and_4_out, one_bit_comparator_1_e, one_bit_comparator_2_e, one_bit_comparator_3_e, one_bit_comparator_4_e, one_bit_comparator_5_g);
  and and_5 (and_5_out, one_bit_comparator_1_e, one_bit_comparator_2_e, one_bit_comparator_4_e, one_bit_comparator_5_e, one_bit_comparator_6_g);
  or or_1 (A_B, one_bit_comparator_1_g, and_1_out, and_2_out, and_3_out, and_4_out, and_5_out);
endmodule
