// Logisim project Modified Circuit.circ as structural Verilog: 8 circuits, main circuit main
module main (
  input  in_1,
  input  item1,
  input  in_3,
  input  Ready_Button,
  input  item2,
  input  in_6,
  input  in_7,
  input  Priority_button,
  output [3:0] out_9,
  output [3:0] Normal_Cost,
  output [2:0] out_11,
  output [3:0] out_12,
  output [1:0] out_13,
  output [2:0] Cost_Returned
);

  wire and_5_out, button_1_out, n4_bit_comparator_1_a_b, n4_bit_up_counter_2_out_3,
       n4_bit_up_counter_2_out_4, n4_bit_up_counter_2_out_5, n4_bit_up_counter_2_s0, xor_1_out;

  and and_1 (out_11[1], item2, Priority_button);
  _4_Bit_Adder u_4_bit_adder_1 (
    .B3(in_1), .A3(item1), .B2(item2), .A2(in_1), .B1(in_1), .A1(item1), .B0(item2), .A0(in_1),
    .S3(Normal_Cost[3]), .S2(Normal_Cost[2]), .S1(Normal_Cost[1]), .S0(Normal_Cost[0]));  // open: Carry
  and and_2 (out_11[2], item1, Priority_button);
  _4_Bit_Adder u_4_bit_adder_2 (
    .B3(in_1), .A3(in_1), .B2(in_1), .A2(item1), .B1(item2), .A1(in_1), .B0(item2), .A0(item1),
    .S3(out_12[3]), .S2(out_12[2]), .S1(out_12[1]), .S0(out_12[0]));  // open: Carry
  and and_3 (Cost_Returned[2], item1, n4_bit_comparator_1_a_b);
  xor xor_1 (xor_1_out, Ready_Button, Priority_button);
  Button button_1 (.out(button_1_out));
  and and_4 (Cost_Returned[1], item2, n4_bit_comparator_1_a_b);
  and and_5 (and_5_out, xor_1_out, button_1_out);
  _4_bit_up_counter u_4_bit_up_counter_1 (
    .in_1(Ready_Button), .in_2(in_3), .out_3(out_9[3]), .out_4(out_9[2]), .out_5(out_9[1]), .S0(out_9[0]));
  _4_bit_up_counter u_4_bit_up_counter_2 (
    .in_1(and_5_out), .in_2(in_6), .out_3(n4_bit_up_counter_2_out_3), .out_4(n4_bit_up_counter_2_out_4),
    .out_5(n4_bit_up_counter_2_out_5), .S0(n4_bit_up_counter_2_s0));
  _4_bit_comparator u_4_bit_comparator_1 (
    .B3(in_7), .A3(n4_bit_up_counter_2_out_3), .B2(out_11[2]), .A2(n4_bit_up_counter_2_out_4),
    .B1(out_11[1]), .A1(n4_bit_up_counter_2_out_5), .B0(in_1), .A0(n4_bit_up_counter_2_s0),
    .A_B(n4_bit_comparator_1_a_b));

  assign Cost_Returned[0] = Cost_Returned[2];
  assign out_11[0] = in_1;
  assign out_13 = out_11[2:1];

  // Notes on the sheet:
  //   4-Bit Adder
  //   Reduced Time
  //   4-Bit Adder
  //   Priority Fee
  //   Normal Time
  //   4-Bit UP Counter
  //   4-Bit UP Counter
  //   4-Bit Comparator
  //   Total Orders 
  //   PRIORITY-DINE
  //   S2-T14
  //   Mithun Patil V N 231CS234
  //   Pranav Venkat YK 231CS242
  //   Yashwanth R 231CS265
endmodule

module _4_Bit_Adder (
  input  B3,
  input  A3,
  input  B2,
  input  A2,
  input  B1,
  input  A1,
  input  B0,
  input  A0,
  output Carry,
  output S3,
  output S2,
  output S1,
  output S0
);

  wire full_adder_2_carry, full_adder_3_carry, half_adder_1_carry;

  full_adder full_adder_1 (.A(A3), .B(B3), .C(full_adder_2_carry), .Sum(S3), .Carry(Carry));
  full_adder full_adder_2 (.A(A2), .B(B2), .C(full_adder_3_carry), .Sum(S2), .Carry(full_adder_2_carry));
  full_adder full_adder_3 (.A(A1), .B(B1), .C(half_adder_1_carry), .Sum(S1), .Carry(full_adder_3_carry));
  half_adder half_adder_1 (.A(A0), .B(B0), .Sum(S0), .Carry(half_adder_1_carry));
endmodule

module full_adder (
  input  A,
  input  B,
  input  C,
  output Sum,
  output Carry
);

  wire and_1_out, and_2_out, xor_1_out;

  xor xor_1 (xor_1_out, A, B);
  and and_1 (and_1_out, A, B);
  xor xor_2 (Sum, xor_1_out, C);
  and and_2 (and_2_out, xor_1_out, C);
  or or_1 (Carry, and_2_out, and_1_out);
endmodule

module half_adder (
  input  A,
  input  B,
  output Sum,
  output Carry
);

  xor xor_1 (Sum, A, B);
  and and_1 (Carry, B, A);
endmodule

module _2_bit_adder (
  input  B1,
  input  A1,
  input  B0,
  input  A0,
  output Carry,
  output S1,
  output S0
);

  wire half_adder_1_carry;

  full_adder full_adder_1 (.A(A1), .B(B1), .C(half_adder_1_carry), .Sum(S1), .Carry(Carry));
  half_adder half_adder_1 (.A(A0), .B(B0), .Sum(S0), .Carry(half_adder_1_carry));
endmodule

module _4_bit_up_counter (
  input  in_1,
  input  in_2,
  output out_3,
  output out_4,
  output out_5,
  output S0
);

  wire j_k_ff_1_qn, j_k_ff_2_qn, j_k_ff_3_qn;

  J_K_Flip_Flop j_k_ff_1 (
    .J(1'b1), .clk(in_1), .K(1'b1), .Q(S0), .Qn(j_k_ff_1_qn), .preset(in_2), .reset(in_2));  // open: en
  J_K_Flip_Flop j_k_ff_2 (
    .J(1'b1), .clk(j_k_ff_1_qn), .K(1'b1), .Q(out_5), .Qn(j_k_ff_2_qn), .preset(in_2), .reset(in_2));  // open: en
  J_K_Flip_Flop j_k_ff_3 (
    .J(1'b1), .clk(j_k_ff_2_qn), .K(1'b1), .Q(out_4), .Qn(j_k_ff_3_qn), .preset(in_2), .reset(in_2));  // open: en
  J_K_Flip_Flop j_k_ff_4 (
    .J(1'b1), .clk(j_k_ff_3_qn), .K(1'b1), .Q(out_3), .preset(in_2), .reset(in_2));  // open: Qn, en
endmodule

module _4_bit_comparator (
  input  B3,
  input  A3,
  input  B2,
  input  A2,
  input  B1,
  input  A1,
  input  B0,
  input  A0,
  output A_B
);

  wire and_1_out, and_2_out, and_3_out, n1_bit_comparator_1_a_b, n1_bit_comparator_1_a_b_3,
       n1_bit_comparator_2_a_b, n1_bit_comparator_2_a_b_3, n1_bit_comparator_3_a_b,
       n1_bit_comparator_3_a_b_3, n1_bit_comparator_4_a_b_3;

  _1_bit_Comparator u_1_bit_comparator_1 (
    .A(A3), .B(B3), .A_B(n1_bit_comparator_1_a_b), .A_B_3(n1_bit_comparator_1_a_b_3));  // open: A_B_2
  _1_bit_Comparator u_1_bit_comparator_2 (
    .A(A2), .B(B2), .A_B(n1_bit_comparator_2_a_b), .A_B_3(n1_bit_comparator_2_a_b_3));  // open: A_B_2
  _1_bit_Comparator u_1_bit_comparator_3 (
    .A(A1), .B(B1), .A_B(n1_bit_comparator_3_a_b), .A_B_3(n1_bit_comparator_3_a_b_3));  // open: A_B_2
  _1_bit_Comparator u_1_bit_comparator_4 (.A(A0), .B(B0), .A_B_3(n1_bit_comparator_4_a_b_3));  // open: A_B, A_B_2
  and and_1 (and_1_out, n1_bit_comparator_1_a_b, n1_bit_comparator_2_a_b_3);
  and and_2 (and_2_out, n1_bit_comparator_1_a_b, n1_bit_comparator_2_a_b, n1_bit_comparator_3_a_b_3);
  and and_3 (and_3_out, n1_bit_comparator_2_a_b, n1_bit_comparator_3_a_b, n1_bit_comparator_4_a_b_3);
  or or_1 (A_B, n1_bit_comparator_1_a_b_3, and_1_out, and_2_out, and_3_out);
endmodule

module _1_bit_Comparator (
  input  A,
  input  B,
  output A_B,
  output A_B_2,
  output A_B_3
);

  wire not_1_out, not_2_out;

  not not_1 (not_1_out, B);
  not not_2 (not_2_out, A);
  xnor xnor_1 (A_B, A, B);
  and and_1 (A_B_2, not_2_out, B);
  and and_2 (A_B_3, A, not_1_out);
endmodule
