// Logisim project S2-T14.circ as structural Verilog: 21 circuits, main circuit One Bit comparator
module One_Bit_comparator (
  input  A,
  input  B,
  output A_B,
  output A_B_2,
  output A_B_3
);

  wire not_1_out, not_2_out;

  not not_1 (not_1_out, B);
  not not_2 (not_2_out, A);
  xnor xnor_1 (A_B, A, B);
  and and_1 (A_B_2, not_2_out, B);
  and and_2 (A_B_3, A, not_1_out);
endmodule

module Two_Bit_Comparator (
  input  B0,
  input  A0,
  input  B1,
  input  A1,
  output A_B,
  output A_B_2,
  output A_B_3
);

  wire and_2_out, and_3_out, one_bit_comparator_1_a_b, one_bit_comparator_1_a_b_2,
       one_bit_comparator_1_a_b_3, one_bit_comparator_2_a_b, one_bit_comparator_2_a_b_2,
       one_bit_comparator_2_a_b_3;

  One_Bit_comparator one_bit_comparator_1 (
    .A(A0), .B(B0), .A_B(one_bit_comparator_1_a_b), .A_B_2(one_bit_comparator_1_a_b_2),
    .A_B_3(one_bit_comparator_1_a_b_3));
  One_Bit_comparator one_bit_comparator_2 (
    .A(A1), .B(B1), .A_B(one_bit_comparator_2_a_b), .A_B_2(one_bit_comparator_2_a_b_2),
    .A_B_3(one_bit_comparator_2_a_b_3));
  and and_1 (A_B, one_bit_comparator_2_a_b, one_bit_comparator_1_a_b);
  and and_2 (and_2_out, one_bit_comparator_2_a_b, one_bit_comparator_1_a_b_2);
  and and_3 (and_3_out, one_bit_comparator_2_a_b, one_bit_comparator_1_a_b_3);
  or or_1 (A_B_2, and_2_out, one_bit_comparator_2_a_b_2);
  or or_2 (A_B_3, and_3_out, one_bit_comparator_2_a_b_3);
endmodule

module _6_Bit_Adder (
  input  B5,
  input  A5,
  input  B4,
  input  A4,
  input  B3,
  input  A3,
  input  B2,
  input  A2,
  input  B1,
  input  A1,
  input  B0,
  input  A0,
  output Carry,
  output S5,
  output S4,
  output S3,
  output S2,
  output S1,
  output S0
);

  wire full_adder_2_carry, full_adder_3_carry, full_adder_4_carry, full_adder_5_carry, half_adder_1_carry;

  Full_Adder full_adder_1 (.A(A5), .B(B5), .C(full_adder_2_carry), .Sum(S5), .Carry(Carry));
  Full_Adder full_adder_2 (.A(A4), .B(B4), .C(full_adder_3_carry), .Sum(S4), .Carry(full_adder_2_carry));
  Full_Adder full_adder_3 (.A(A3), .B(B3), .C(full_adder_4_carry), .Sum(S3), .Carry(full_adder_3_carry));
  Full_Adder full_adder_4 (.A(A2), .B(B2), .C(full_adder_5_carry), .Sum(S2), .Carry(full_adder_4_carry));
  Full_Adder full_adder_5 (.A(A1), .B(B1), .C(half_adder_1_carry), .Sum(S1), .Carry(full_adder_5_carry));
  Half_Adder half_adder_1 (.A(A0), .B(B0), .Sum(S0), .Carry(half_adder_1_carry));
endmodule

module Full_Adder (
  input  A,
  input  B,
  input  C,
  output Sum,
  output Carry
);

  wire and_1_out, and_2_out, xor_1_out;

  xor xor_1 (xor_1_out, A, B);
  and and_1 (and_1_out, A, B);
  xor xor_2 (Sum, xor_1_out, C);
  and and_2 (and_2_out, xor_1_out, C);
  or or_1 (Carry, and_2_out, and_1_out);
endmodule

module _4_Bit_Down_Counter (
  input  Clock,
  input  J__K,
  input  Preset,
  input  Clear,
  output out_5,
  output out_6,
  output out_7,
  output out_8
);

  wire j_k_ff_1_qn, j_k_ff_2_qn, j_k_ff_3_qn;

  J_K_Flip_Flop #(.trigger("falling")) j_k_ff_1 (
    .J(J__K), .clk(Clock), .K(J__K), .Q(out_8), .Qn(j_k_ff_1_qn), .preset(Clear), .reset(Preset));  // open: en
  J_K_Flip_Flop #(.trigger("falling")) j_k_ff_2 (
    .J(J__K), .clk(j_k_ff_1_qn), .K(J__K), .Q(out_7), .Qn(j_k_ff_2_qn), .preset(Clear), .reset(Preset));  // open: en
  J_K_Flip_Flop #(.trigger("falling")) j_k_ff_3 (
    .J(J__K), .clk(j_k_ff_2_qn), .K(J__K), .Q(out_6), .Qn(j_k_ff_3_qn), .preset(Clear), .reset(Preset));  // open: en
  J_K_Flip_Flop #(.trigger("falling")) j_k_ff_4 (
    .J(J__K), .clk(j_k_ff_3_qn), .K(J__K), .Q(out_5), .preset(Clear), .reset(Preset));  // open: Qn, en
endmodule

module _5_Bit_Up_Counter (
  input  J__K,
  input  Preset__Clear,
  output out_3,
  output out_4,
  output out_5,
  output out_6,
  output LSB
);

  wire Clock_out, j_k_ff_1_qn, j_k_ff_2_qn, j_k_ff_3_qn, j_k_ff_4_qn;

  Clock Clock (.out(Clock_out));
  J_K_Flip_Flop j_k_ff_1 (
    .J(J__K), .clk(Clock_out), .K(J__K), .Q(LSB), .Qn(j_k_ff_1_qn), .preset(Preset__Clear),
    .reset(Preset__Clear));  // open: en
  J_K_Flip_Flop j_k_ff_2 (
    .J(J__K), .clk(j_k_ff_1_qn), .K(J__K), .Q(out_6), .Qn(j_k_ff_2_qn), .preset(Preset__Clear),
    .reset(Preset__Clear));  // open: en
  J_K_Flip_Flop j_k_ff_3 (
    .J(J__K), .clk(j_k_ff_2_qn), .K(J__K), .Q(out_5), .Qn(j_k_ff_3_qn), .preset(Preset__Clear),
    .reset(Preset__Clear));  // open: en
  J_K_Flip_Flop j_k_ff_4 (
    .J(J__K), .clk(j_k_ff_3_qn), .K(J__K), .Q(out_4), .Qn(j_k_ff_4_qn), .preset(Preset__Clear),
    .reset(Preset__Clear));  // open: en
  J_K_Flip_Flop j_k_ff_5 (
    .J(J__K), .clk(j_k_ff_4_qn), .K(J__K), .Q(out_3), .preset(Preset__Clear), .reset(Preset__Clear));  // open: Qn, en
endmodule

module Half_Adder (
  input  A,
  input  B,
  output Sum,
  output Carry
);

  xor xor_1 (Sum, A, B);
  and and_1 (Carry, B, A);
endmodule

module _5_by_2_Multiplier (
  input  A4,
  input  A3,
  input  A2,
  input  A1,
  input  A0,
  input  B0,
  input  B1,
  output S5,
  output S4,
  output S3,
  output S2,
  output S1,
  output S0
);

  wire and_1_out, and_2_out, and_3_out, and_4_out, and_5_out, and_6_out, and_7_out, and_8_out, and_9_out,
       full_adder_1_carry, full_adder_2_carry, full_adder_3_carry, half_adder_2_carry;

  and and_1 (and_1_out, B0, A4);
  and and_2 (and_2_out, B1, A4);
  Half_Adder half_adder_1 (.A(full_adder_1_carry), .B(and_2_out), .Sum(S5));  // open: Carry
  and and_3 (and_3_out, B0, A3);
  and and_4 (and_4_out, B1, A3);
  Full_Adder full_adder_1 (.A(full_adder_2_carry), .B(and_4_out), .C(and_1_out), .Sum(S4), .Carry(full_adder_1_carry));
  Full_Adder full_adder_2 (.A(full_adder_3_carry), .B(and_6_out), .C(and_3_out), .Sum(S3), .Carry(full_adder_2_carry));
  and and_5 (and_5_out, B0, A2);
  and and_6 (and_6_out, B1, A2);
  Full_Adder full_adder_3 (.A(half_adder_2_carry), .B(and_9_out), .C(and_5_out), .Sum(S2), .Carry(full_adder_3_carry));
  and and_7 (and_7_out, B0, A1);
  and and_8 (and_8_out, B1, A0);
  and and_9 (and_9_out, B1, A1);
  Half_Adder half_adder_2 (.A(and_8_out), .B(and_7_out), .Sum(S1), .Carry(half_adder_2_carry));
  and and_10 (S0, B0, A0);
endmodule

module _2_bit_Up_Counter (
  input  Clock,
  input  J__K,
  input  Preset__Clear,
  output out_4,
  output out_5
);

  wire j_k_ff_1_qn;

  J_K_Flip_Flop #(.trigger("falling")) j_k_ff_1 (
    .J(J__K), .clk(Clock), .K(J__K), .Q(out_5), .Qn(j_k_ff_1_qn), .preset(Preset__Clear),
    .reset(Preset__Clear));  // open: en
  J_K_Flip_Flop j_k_ff_2 (
    .J(J__K), .clk(j_k_ff_1_qn), .K(J__K), .Q(out_4), .preset(Preset__Clear), .reset(Preset__Clear));  // open: Qn, en
endmodule

module _3_by_2_Multiplier (
  input  A2,
  input  A1,
  input  A0,
  input  B0,
  input  B1,
  output S3,
  output S2,
  output S1,
  output S0
);

  wire and_1_out, and_2_out, and_3_out, and_4_out, and_5_out, full_adder_1_carry, half_adder_2_carry;

  Half_Adder half_adder_1 (.A(full_adder_1_carry), .B(and_2_out), .Sum(S3));  // open: Carry
  and and_1 (and_1_out, B0, A2);
  and and_2 (and_2_out, B1, A2);
  Full_Adder full_adder_1 (.A(half_adder_2_carry), .B(and_4_out), .C(and_1_out), .Sum(S2), .Carry(full_adder_1_carry));
  and and_3 (and_3_out, B0, A1);
  and and_4 (and_4_out, B1, A1);
  and and_5 (and_5_out, B1, A0);
  Half_Adder half_adder_2 (.A(and_5_out), .B(and_3_out), .Sum(S1), .Carry(half_adder_2_carry));
  and and_6 (S0, B0, A0);
endmodule

module _7_Bit_Up_Counter (
  input  J__K,
  input  Preset__Clear,
  input  Clock,
  output out_4,
  output out_5,
  output out_6,
  output out_7,
  output out_8,
  output out_9,
  output out_10
);

  wire j_k_ff_2_qn, j_k_ff_3_qn, j_k_ff_4_qn, j_k_ff_5_qn, j_k_ff_6_qn, j_k_ff_7_qn;

  J_K_Flip_Flop j_k_ff_1 (
    .J(J__K), .clk(j_k_ff_2_qn), .K(J__K), .Q(out_4), .preset(Preset__Clear), .reset(Preset__Clear));  // open: Qn, en
  J_K_Flip_Flop j_k_ff_2 (
    .J(J__K), .clk(j_k_ff_3_qn), .K(J__K), .Q(out_5), .Qn(j_k_ff_2_qn), .preset(Preset__Clear),
    .reset(Preset__Clear));  // open: en
  J_K_Flip_Flop j_k_ff_3 (
    .J(J__K), .clk(j_k_ff_4_qn), .K(J__K), .Q(out_6), .Qn(j_k_ff_3_qn), .preset(Preset__Clear),
    .reset(Preset__Clear));  // open: en
  J_K_Flip_Flop j_k_ff_4 (
    .J(J__K), .clk(j_k_ff_5_qn), .K(J__K), .Q(out_7), .Qn(j_k_ff_4_qn), .preset(Preset__Clear),
    .reset(Preset__Clear));  // open: en
  J_K_Flip_Flop j_k_ff_5 (
    .J(J__K), .clk(j_k_ff_6_qn), .K(J__K), .Q(out_8), .Qn(j_k_ff_5_qn), .preset(Preset__Clear),
    .reset(Preset__Clear));  // open: en
  J_K_Flip_Flop j_k_ff_6 (
    .J(J__K), .clk(j_k_ff_7_qn), .K(J__K), .Q(out_9), .Qn(j_k_ff_6_qn), .preset(Preset__Clear),
    .reset(Preset__Clear));  // open: en
  J_K_Flip_Flop #(.trigger("falling")) j_k_ff_7 (
    .J(J__K), .clk(Clock), .K(J__K), .Q(out_10), .Qn(j_k_ff_7_qn), .preset(Preset__Clear),
    .reset(Preset__Clear));  // open: en
endmodule

module Divide_by_2 (
  input  A6,
  input  A5,
  input  A4,
  input  A3,
  input  A2,
  input  A1,
  input  A0,
  output B0,
  output B1,
  output B2,
  output B3,
  output B4,
  output B5
);


  assign B0 = A1;
  assign B1 = A2;
  assign B2 = A3;
  assign B3 = A4;
  assign B4 = A5;
  assign B5 = A6;
endmodule

module Divide_by_10 (
  input  A6,
  input  A5,
  input  A4,
  input  A3,
  input  A2,
  input  A1,
  input  A0,
  output B0,
  output B1,
  output B2,
  output B3
);


  assign B0 = A3;
  assign B1 = A4;
  assign B2 = A5;
  assign B3 = A6;

  // Notes on the sheet:
  //   This is the logisim part for the 12.5% of the cost.
endmodule

module Full_Subtractor (
  input  A,
  input  B,
  input  C,
  output Difference,
  output Borrow
);

  wire and_1_out, and_2_out, not_1_out, not_2_out, xor_1_out;

  xor xor_1 (xor_1_out, A, B);
  xor xor_2 (Difference, xor_1_out, C);
  not not_1 (not_1_out, xor_1_out);
  not not_2 (not_2_out, A);
  and and_1 (and_1_out, not_1_out, C);
  and and_2 (and_2_out, not_2_out, B);
  or or_1 (Borrow, and_1_out, and_2_out);
endmodule

module Subtract_by_1 (
  input  A2,
  input  A1,
  input  A0,
  input  in_4,
  input  in_5,
  output out_6,
  output out_7,
  output out_8
);

  wire full_subtractor_2_borrow, full_subtractor_3_borrow;

  Full_Subtractor full_subtractor_1 (
    .A(A2), .B(in_5), .C(full_subtractor_2_borrow), .Difference(out_6));  // open: Borrow
  Full_Subtractor full_subtractor_2 (
    .A(A1), .B(in_5), .C(full_subtractor_3_borrow), .Difference(out_7), .Borrow(full_subtractor_2_borrow));
  Full_Subtractor full_subtractor_3 (.A(A0), .B(in_4), .C(in_5), .Difference(out_8), .Borrow(full_subtractor_3_borrow));
endmodule

module _4_Bit_Adder (
  input  B3,
  input  A3,
  input  B2,
  input  A2,
  input  B1,
  input  A1,
  input  B0,
  input  A0,
  output Carry,
  output S3,
  output S2,
  output S1,
  output S0
);

  wire full_adder_2_carry, full_adder_3_carry, half_adder_1_carry;

  Full_Adder full_adder_1 (.A(A3), .B(B3), .C(full_adder_2_carry), .Sum(S3), .Carry(Carry));
  Full_Adder full_adder_2 (.A(A2), .B(B2), .C(full_adder_3_carry), .Sum(S2), .Carry(full_adder_2_carry));
  Full_Adder full_adder_3 (.A(A1), .B(B1), .C(half_adder_1_carry), .Sum(S1), .Carry(full_adder_3_carry));
  Half_Adder half_adder_1 (.A(A0), .B(B0), .Sum(S0), .Carry(half_adder_1_carry));
endmodule

module _5_Bit_Adder (
  input  B4,
  input  A4,
  input  B3,
  input  A3,
  input  B2,
  input  A2,
  input  B1,
  input  A1,
  input  B0,
  input  A0,
  output Carry,
  output S4,
  output S3,
  output S2,
  output S1,
  output S0
);

  wire full_adder_2_carry, full_adder_3_carry, full_adder_4_carry, half_adder_1_carry;

  Full_Adder full_adder_1 (.A(A4), .B(B4), .C(full_adder_2_carry), .Sum(S4), .Carry(Carry));
  Full_Adder full_adder_2 (.A(A3), .B(B3), .C(full_adder_3_carry), .Sum(S3), .Carry(full_adder_2_carry));
  Full_Adder full_adder_3 (.A(A2), .B(B2), .C(full_adder_4_carry), .Sum(S2), .Carry(full_adder_3_carry));
  Full_Adder full_adder_4 (.A(A1), .B(B1), .C(half_adder_1_carry), .Sum(S1), .Carry(full_adder_4_carry));
  Half_Adder half_adder_1 (.A(A0), .B(B0), .Sum(S0), .Carry(half_adder_1_carry));
endmodule

module _6_Bit_Comparator (
  input  B5,
  input  A5,
  input  B4,
  input  A4,
  input  B3,
  input  A3,
  input  B2,
  input  A2,
  input  B1,
  input  A1,
  input  B0,
  input  A0,
  output A_B
);

  wire and_1_out, and_2_out, and_3_out, and_4_out, and_5_out, one_bit_comparator_1_a_b,
       one_bit_comparator_1_a_b_3, one_bit_comparator_2_a_b, one_bit_comparator_2_a_b_3,
       one_bit_comparator_3_a_b, one_bit_comparator_3_a_b_3, one_bit_comparator_4_a_b,
       one_bit_comparator_4_a_b_3, one_bit_comparator_5_a_b, one_bit_comparator_5_a_b_3,
       one_bit_comparator_6_a_b_3;

  One_Bit_comparator one_bit_comparator_1 (
    .A(A5), .B(B5), .A_B(one_bit_comparator_1_a_b), .A_B_3(one_bit_comparator_1_a_b_3));  // open: A_B_2
  One_Bit_comparator one_bit_comparator_2 (
    .A(A4), .B(B4), .A_B(one_bit_comparator_2_a_b), .A_B_3(one_bit_comparator_2_a_b_3));  // open: A_B_2
  One_Bit_comparator one_bit_comparator_3 (
    .A(A3), .B(B3), .A_B(one_bit_comparator_3_a_b), .A_B_3(one_bit_comparator_3_a_b_3));  // open: A_B_2
  One_Bit_comparator one_bit_comparator_4 (
    .A(A2), .B(B2), .A_B(one_bit_comparator_4_a_b), .A_B_3(one_bit_comparator_4_a_b_3));  // open: A_B_2
  One_Bit_comparator one_bit_comparator_5 (
    .A(A1), .B(B1), .A_B(one_bit_comparator_5_a_b), .A_B_3(one_bit_comparator_5_a_b_3));  // open: A_B_2
  One_Bit_comparator one_bit_comparator_6 (.A(A0), .B(B0), .A_B_3(one_bit_comparator_6_a_b_3));  // open: A_B, A_B_2
  and and_1 (and_1_out, one_bit_comparator_1_a_b, one_bit_comparator_2_a_b_3);
  and and_2 (and_2_out, one_bit_comparator_1_a_b, one_bit_comparator_2_a_b, one_bit_comparator_3_a_b_3);
  and and_3 (and_3_out, one_bit_comparator_1_a_b, one_bit_comparator_2_a_b, one_bit_comparator_3_a_b, one_bit_comparator_4_a_b_3);
  and and_4 (and_4_out, one_bit_comparator_1_a_b, one_bit_comparator_2_a_b, one_bit_comparator_3_a_b, one_bit_comparator_4_a_b, one_bit_comparator_5_a_b_3);
  and and_5 (and_5_out, one_bit_comparator_1_a_b, one_bit_comparator_2_a_b, one_bit_comparator_4_a_b, one_bit_comparator_5_a_b, one_bit_comparator_6_a_b_3);
  or or_1 (A_B, one_bit_comparator_1_a_b_3, and_1_out, and_2_out, and_3_out, and_4_out, and_5_out);
endmodule

module Normal_Service (
  input  Start_Button,
  input  in_2,
  input  in_3,
  input  in_4,
  input  in_5,
  input  in_6,
  input  Item_1,
  input  Ready_Button,
  input  Item_2,
  input  PriorityS,
  input  PrioriySL,
  input  in_12,
  input  Item_3,
  input  Item_4,
  input  Ready_Button_2,
  input  PriorityM,
  input  PriorityML,
  input  in_18,
  input  in_19,
  input  in_20,
  input  in_21,
  input  Item_5,
  input  Item_6,
  input  Ready_Button_3,
  input  PriorityJ,
  input  PriorityJL,
  output [6:0] Total_Cost_of_the_items,
  output [4:0] Total_Estimated_Time_to_prepare,
  output [3:0] Estimated_time_to_prepare_the_item_in_each_section
);

  wire and_1_out, and_2_out, and_3_out, and_4_out, and_5_out, and_6_out, and_7_out, and_8_out, and_9_out,
       and_10_out, and_11_out, and_12_out, half_adder_1_carry, half_adder_1_sum, half_adder_2_carry,
       half_adder_2_sum, half_adder_3_carry, half_adder_3_sum, n2_bit_up_counter_1_out_4,
       n2_bit_up_counter_1_out_5, n3_by_2_multiplier_1_s0, n3_by_2_multiplier_1_s1, n3_by_2_multiplier_1_s2,
       n3_by_2_multiplier_1_s3, n3_by_2_multiplier_2_s0, n3_by_2_multiplier_2_s1, n3_by_2_multiplier_2_s2,
       n3_by_2_multiplier_2_s3, n3_by_2_multiplier_3_s0, n3_by_2_multiplier_3_s1, n3_by_2_multiplier_3_s2,
       n3_by_2_multiplier_3_s3, n4_bit_adder_1_carry, n4_bit_adder_1_s0, n4_bit_adder_1_s1,
       n4_bit_adder_1_s2, n4_bit_adder_1_s3, n4_bit_adder_2_carry, n5_by_2_multiplier_1_s0,
       n5_by_2_multiplier_1_s1, n5_by_2_multiplier_1_s2, n5_by_2_multiplier_1_s3, n5_by_2_multiplier_1_s4,
       n5_by_2_multiplier_1_s5, n5_by_2_multiplier_2_s0, n5_by_2_multiplier_2_s1, n5_by_2_multiplier_2_s2,
       n5_by_2_multiplier_2_s3, n5_by_2_multiplier_2_s4, n5_by_2_multiplier_2_s5, n5_by_2_multiplier_3_s0,
       n5_by_2_multiplier_3_s1, n5_by_2_multiplier_3_s2, n5_by_2_multiplier_3_s3, n5_by_2_multiplier_3_s4,
       n5_by_2_multiplier_3_s5, n6_bit_adder_1_carry, n6_bit_adder_1_s0, n6_bit_adder_1_s1,
       n6_bit_adder_1_s2, n6_bit_adder_1_s3, n6_bit_adder_1_s4, n6_bit_adder_1_s5, n6_bit_adder_2_carry,
       or_3_out, two_bit_comparator_1_a_b, two_bit_comparator_2_a_b, two_bit_comparator_3_a_b;

  Half_Adder half_adder_1 (.A(Item_3), .B(Item_4), .Sum(half_adder_1_sum), .Carry(half_adder_1_carry));
  _5_by_2_Multiplier u_5_by_2_multiplier_1 (
    .B0(half_adder_2_sum), .B1(half_adder_2_carry), .A4(in_18), .A3(1'b1), .A2(in_19), .A1(1'b1), .A0(in_20),
    .S5(n5_by_2_multiplier_1_s5), .S4(n5_by_2_multiplier_1_s4), .S3(n5_by_2_multiplier_1_s3),
    .S2(n5_by_2_multiplier_1_s2), .S1(n5_by_2_multiplier_1_s1), .S0(n5_by_2_multiplier_1_s0));
  Half_Adder half_adder_2 (.A(Item_5), .B(Item_6), .Sum(half_adder_2_sum), .Carry(half_adder_2_carry));
  Half_Adder half_adder_3 (.A(Item_1), .B(Item_2), .Sum(half_adder_3_sum), .Carry(half_adder_3_carry));
  _5_by_2_Multiplier u_5_by_2_multiplier_2 (
    .B0(half_adder_1_sum), .B1(half_adder_1_carry), .A4(1'b1), .A3(1'b1), .A2(1'b1), .A1(1'b1), .A0(in_12),
    .S5(n5_by_2_multiplier_2_s5), .S4(n5_by_2_multiplier_2_s4), .S3(n5_by_2_multiplier_2_s3),
    .S2(n5_by_2_multiplier_2_s2), .S1(n5_by_2_multiplier_2_s1), .S0(n5_by_2_multiplier_2_s0));
  _6_Bit_Adder u_6_bit_adder_1 (
    .B5(n5_by_2_multiplier_2_s5), .A5(n5_by_2_multiplier_3_s5), .B4(n5_by_2_multiplier_2_s4),
    .A4(n5_by_2_multiplier_3_s4), .B3(n5_by_2_multiplier_2_s3), .A3(n5_by_2_multiplier_3_s3),
    .B2(n5_by_2_multiplier_2_s2), .A2(n5_by_2_multiplier_3_s2), .B1(n5_by_2_multiplier_2_s1),
    .A1(n5_by_2_multiplier_3_s1), .B0(n5_by_2_multiplier_2_s0), .A0(n5_by_2_multiplier_3_s0),
    .Carry(n6_bit_adder_1_carry), .S5(n6_bit_adder_1_s5), .S4(n6_bit_adder_1_s4), .S3(n6_bit_adder_1_s3),
    .S2(n6_bit_adder_1_s2), .S1(n6_bit_adder_1_s1), .S0(n6_bit_adder_1_s0));
  _6_Bit_Adder u_6_bit_adder_2 (
    .B5(n5_by_2_multiplier_1_s5), .A5(n6_bit_adder_1_s5), .B4(n5_by_2_multiplier_1_s4),
    .A4(n6_bit_adder_1_s4), .B3(n5_by_2_multiplier_1_s3), .A3(n6_bit_adder_1_s3),
    .B2(n5_by_2_multiplier_1_s2), .A2(n6_bit_adder_1_s2), .B1(n5_by_2_multiplier_1_s1),
    .A1(n6_bit_adder_1_s1), .B0(n5_by_2_multiplier_1_s0), .A0(n6_bit_adder_1_s0),
    .Carry(n6_bit_adder_2_carry), .S5(Total_Cost_of_the_items[5]), .S4(Total_Cost_of_the_items[4]),
    .S3(Total_Cost_of_the_items[3]), .S2(Total_Cost_of_the_items[2]), .S1(Total_Cost_of_the_items[1]),
    .S0(Total_Cost_of_the_items[0]));
  or or_1 (Total_Cost_of_the_items[6], n6_bit_adder_1_carry, n6_bit_adder_2_carry);
  _5_by_2_Multiplier u_5_by_2_multiplier_3 (
    .B0(half_adder_3_sum), .B1(half_adder_3_carry), .A4(1'b1), .A3(in_4), .A2(1'b1), .A1(in_5), .A0(in_6),
    .S5(n5_by_2_multiplier_3_s5), .S4(n5_by_2_multiplier_3_s4), .S3(n5_by_2_multiplier_3_s3),
    .S2(n5_by_2_multiplier_3_s2), .S1(n5_by_2_multiplier_3_s1), .S0(n5_by_2_multiplier_3_s0));
  _3_by_2_Multiplier u_3_by_2_multiplier_1 (
    .B0(half_adder_3_sum), .B1(half_adder_3_carry), .A2(1'b1), .A1(in_3), .A0(1'b1),
    .S3(n3_by_2_multiplier_1_s3), .S2(n3_by_2_multiplier_1_s2), .S1(n3_by_2_multiplier_1_s1),
    .S0(n3_by_2_multiplier_1_s0));
  _3_by_2_Multiplier u_3_by_2_multiplier_2 (
    .B0(half_adder_1_sum), .B1(half_adder_1_carry), .A2(1'b1), .A1(1'b1), .A0(1'b1),
    .S3(n3_by_2_multiplier_2_s3), .S2(n3_by_2_multiplier_2_s2), .S1(n3_by_2_multiplier_2_s1),
    .S0(n3_by_2_multiplier_2_s0));
  _3_by_2_Multiplier u_3_by_2_multiplier_3 (
    .B0(half_adder_2_sum), .B1(half_adder_2_carry), .A2(in_21), .A1(1'b1), .A0(1'b1),
    .S3(n3_by_2_multiplier_3_s3), .S2(n3_by_2_multiplier_3_s2), .S1(n3_by_2_multiplier_3_s1),
    .S0(n3_by_2_multiplier_3_s0));
  _4_Bit_Adder u_4_bit_adder_1 (
    .B3(n3_by_2_multiplier_2_s3), .A3(n3_by_2_multiplier_1_s3), .B2(n3_by_2_multiplier_2_s2),
    .A2(n3_by_2_multiplier_1_s2), .B1(n3_by_2_multiplier_2_s1), .A1(n3_by_2_multiplier_1_s1),
    .B0(n3_by_2_multiplier_2_s0), .A0(n3_by_2_multiplier_1_s0), .Carry(n4_bit_adder_1_carry),
    .S3(n4_bit_adder_1_s3), .S2(n4_bit_adder_1_s2), .S1(n4_bit_adder_1_s1), .S0(n4_bit_adder_1_s0));
  _4_Bit_Adder u_4_bit_adder_2 (
    .B3(n4_bit_adder_1_s3), .A3(n3_by_2_multiplier_3_s3), .B2(n4_bit_adder_1_s2),
    .A2(n3_by_2_multiplier_3_s2), .B1(n4_bit_adder_1_s1), .A1(n3_by_2_multiplier_3_s1),
    .B0(n4_bit_adder_1_s0), .A0(n3_by_2_multiplier_3_s0), .Carry(n4_bit_adder_2_carry),
    .S3(Total_Estimated_Time_to_prepare[3]), .S2(Total_Estimated_Time_to_prepare[2]),
    .S1(Total_Estimated_Time_to_prepare[1]), .S0(Total_Estimated_Time_to_prepare[0]));
  or or_2 (Total_Estimated_Time_to_prepare[4], n4_bit_adder_1_carry, n4_bit_adder_2_carry);
  _2_bit_Up_Counter u_2_bit_up_counter_1 (
    .Clock(or_3_out), .J__K(1'b1), .Preset__Clear(in_2), .out_4(n2_bit_up_counter_1_out_4),
    .out_5(n2_bit_up_counter_1_out_5));
  Two_Bit_Comparator two_bit_comparator_1 (
    .B0(PriorityS), .A0(n2_bit_up_counter_1_out_4), .B1(PrioriySL), .A1(n2_bit_up_counter_1_out_5),
    .A_B(two_bit_comparator_1_a_b));  // open: A_B_2, A_B_3
  and and_1 (and_1_out, n3_by_2_multiplier_1_s3, two_bit_comparator_1_a_b);
  Two_Bit_Comparator two_bit_comparator_2 (
    .B0(PriorityM), .A0(n2_bit_up_counter_1_out_4), .B1(PriorityML), .A1(n2_bit_up_counter_1_out_5),
    .A_B(two_bit_comparator_2_a_b));  // open: A_B_2, A_B_3
  and and_2 (and_2_out, n3_by_2_multiplier_2_s3, two_bit_comparator_2_a_b);
  Two_Bit_Comparator two_bit_comparator_3 (
    .B0(PriorityJ), .A0(n2_bit_up_counter_1_out_4), .B1(PriorityJL), .A1(n2_bit_up_counter_1_out_5),
    .A_B(two_bit_comparator_3_a_b));  // open: A_B_2, A_B_3
  and and_3 (and_3_out, n3_by_2_multiplier_3_s3, two_bit_comparator_3_a_b);
  or or_3 (or_3_out, Start_Button, Ready_Button_3, Ready_Button, Ready_Button_2);
  and and_4 (and_4_out, n3_by_2_multiplier_1_s2, two_bit_comparator_1_a_b);
  and and_5 (and_5_out, n3_by_2_multiplier_2_s2, two_bit_comparator_2_a_b);
  and and_6 (and_6_out, n3_by_2_multiplier_3_s2, two_bit_comparator_3_a_b);
  and and_7 (and_7_out, n3_by_2_multiplier_1_s0, two_bit_comparator_1_a_b);
  and and_8 (and_8_out, n3_by_2_multiplier_1_s1, two_bit_comparator_1_a_b);
  and and_9 (and_9_out, n3_by_2_multiplier_2_s0, two_bit_comparator_2_a_b);
  and and_10 (and_10_out, n3_by_2_multiplier_2_s1, two_bit_comparator_2_a_b);
  and and_11 (and_11_out, n3_by_2_multiplier_3_s1, two_bit_comparator_3_a_b);
  and and_12 (and_12_out, n3_by_2_multiplier_3_s0, two_bit_comparator_3_a_b);
  or or_4 (Estimated_time_to_prepare_the_item_in_each_section[3], and_3_out, and_2_out, and_1_out);
  or or_5 (Estimated_time_to_prepare_the_item_in_each_section[2], and_6_out, and_5_out, and_4_out);
  or or_6 (Estimated_time_to_prepare_the_item_in_each_section[1], and_11_out, and_10_out, and_8_out);
  or or_7 (Estimated_time_to_prepare_the_item_in_each_section[0], and_12_out, and_9_out, and_7_out);

  // Notes on the sheet:
  //   Starter Section
  //   Main Section
  //   Dessert Section
  //   Half Adder
  //   Half Adder
  //   Cost of each item
  //   Half Adder
  //   Cost of each item
  //   5 by 2
  //   Multiplier
  //   5 by 2
  //   Multiplier
  //   6 Bit Adder
  //   6 Bit Adder
  //   Cost of each item
  //   5 by 2
  //   Multiplier
  //   Estimated Time of each item
  //   Estimated Time of each item
  //   Estimated Time of each item
  //   3 by 2 Multiplier
  //   3 by 2 Multiplier
  //   3 by 2 Multiplier
  //   4 Bit Adder
  //   4 Bit Adder
  //   2 Bit Up Counter
  //   2 Bit Comparator
  //   2 Bit Comparator
  //   2 Bit Comparator
endmodule

module Main_Circuit (
  input  in_1,
  input  Reset_Button,
  input  Start_Button,
  input  in_4,
  input  in_5,
  input  Item_1,
  input  Item_2,
  input  Ready_Button,
  input  in_9,
  input  in_10,
  input  Priority,
  input  in_12,
  input  Item_3,
  input  Item_4,
  input  Ready_Button_2,
  input  in_16,
  input  in_17,
  input  Priority_2,
  input  Item_5,
  input  Item_6,
  input  in_21,
  input  Ready_Button_3,
  input  in_23,
  input  Priority_3,
  input  in_25,
  input  Priority_Service,
  input  in_27,
  output [6:0] Total_Number_of_Orders,
  output [3:0] Available_Stock_of_Item_1,
  output [3:0] Available_Stock_of_Item_2,
  output [3:0] Available_Stock_of_Item_3,
  output [3:0] Available_Stock_of_Item_4,
  output [3:0] Available_Stock_of_Item_5,
  output [3:0] Available_Stock_of_Item_6,
  output [3:0] Estimated_time_to_prepare_the_food_in_the_present_section,
  output [4:0] Total_Estimated_Time_to_prepare,
  output [6:0] Total_Cost_of_the_items,
  output [3:0] Estimated_Time_to_prepare_the_food_in_the_present_Section_2,
  output [4:0] Total_Estimated_Time_to_prepare_2,
  output [5:0] Money_to_be_Returned,
  output [6:0] Total_Cost_of_the_Items_2,
  output [3:0] Priority_Fee
);

  wire and_1_out, and_2_out, and_3_out, and_4_out, and_5_out, and_6_out, and_7_out, and_8_out, not_1_out;

  and and_1 (and_1_out, Start_Button, Priority_Service);
  not not_1 (not_1_out, Priority_Service);
  _7_Bit_Up_Counter u_7_bit_up_counter_1 (
    .J__K(1'b1), .Preset__Clear(in_1), .Clock(Start_Button), .out_4(Total_Number_of_Orders[6]),
    .out_5(Total_Number_of_Orders[5]), .out_6(Total_Number_of_Orders[4]), .out_7(Total_Number_of_Orders[3]),
    .out_8(Total_Number_of_Orders[2]), .out_9(Total_Number_of_Orders[1]), .out_10(Total_Number_of_Orders[0]));
  Normal_Service normal_service_1 (
    .Start_Button(and_2_out), .in_2(in_5), .Item_1(Item_1), .Ready_Button(Ready_Button), .Item_2(Item_2),
    .Item_3(Item_3), .Item_4(Item_4), .Ready_Button_2(Ready_Button_2), .Item_5(Item_5), .Item_6(Item_6),
    .Ready_Button_3(Ready_Button_3), .PriorityS(Priority), .PrioriySL(in_10), .PriorityM(Priority_2),
    .PriorityML(in_16), .PriorityJ(Priority_3), .PriorityJL(in_23), .in_18(in_5), .in_19(in_5), .in_20(in_5),
    .in_12(in_5), .in_4(in_5), .in_5(in_5), .in_6(in_5), .in_21(in_5), .in_3(in_5),
    .Total_Cost_of_the_items(Total_Cost_of_the_items),
    .Total_Estimated_Time_to_prepare(Total_Estimated_Time_to_prepare),
    .Estimated_time_to_prepare_the_item_in_each_section(Estimated_time_to_prepare_the_food_in_the_present_section));
  and and_2 (and_2_out, Start_Button, not_1_out);
  Priority_service priority_service_1 (
    .Start_Button(and_1_out), ._2_Bit_Up(in_27), .in_7(in_27), .Item_1(Item_1), .Ready_Button(Ready_Button),
    .Item_2(Item_2), .Item_3(Item_3), .Item_4(Item_4), .in_17(in_27), .Ready_Button_2(Ready_Button_2),
    .Item_5(Item_5), .Item_6(Item_6), .in_28(in_27), .Ready_Button_3(Ready_Button_3), .in_32(in_27),
    .in_33(in_27), .Priority_Service(Priority_Service), .in_35(in_27), .PriorityS(Priority),
    .PrioriySL(in_10), .PriorityM(Priority_2), .PriorityML(in_16), .PriorityJ(Priority_3),
    .PriorityJL(in_23), .in_22(in_27), ._5_by_2(in_27), .in_24(in_27), .in_14(in_27), .in_4(in_27),
    .in_5(in_27), .in_6(in_27), .in_25(in_27), .in_3(in_27), .in_13(in_27), .in_21(in_27),
    .Priority_Fee(Priority_Fee), .Total_Cost_of_the_items(Total_Cost_of_the_Items_2),
    .Money_to_be_returned(Money_to_be_Returned),
    .Total_Estimated_Time_to_prepare(Total_Estimated_Time_to_prepare_2),
    .Estimated_Time_to_preapre_in_each_section(Estimated_Time_to_prepare_the_food_in_the_present_Section_2));
  and and_3 (and_3_out, Ready_Button, Item_1);
  and and_4 (and_4_out, Ready_Button, Item_2);
  and and_5 (and_5_out, Item_3, Ready_Button_2);
  and and_6 (and_6_out, Item_4, Ready_Button_2);
  and and_7 (and_7_out, Item_5, Ready_Button_3);
  and and_8 (and_8_out, Ready_Button_3, Item_6);
  _4_Bit_Down_Counter u_4_bit_down_counter_1 (
    .Clock(and_3_out), .J__K(1'b1), .Preset(in_4), .Clear(Reset_Button),
    .out_5(Available_Stock_of_Item_1[3]), .out_6(Available_Stock_of_Item_1[2]),
    .out_7(Available_Stock_of_Item_1[1]), .out_8(Available_Stock_of_Item_1[0]));
  _4_Bit_Down_Counter u_4_bit_down_counter_2 (
    .Clock(and_4_out), .J__K(1'b1), .Preset(in_9), .Clear(Reset_Button),
    .out_5(Available_Stock_of_Item_2[3]), .out_6(Available_Stock_of_Item_2[2]),
    .out_7(Available_Stock_of_Item_2[1]), .out_8(Available_Stock_of_Item_2[0]));
  _4_Bit_Down_Counter u_4_bit_down_counter_3 (
    .Clock(and_5_out), .J__K(1'b1), .Preset(in_12), .Clear(Reset_Button),
    .out_5(Available_Stock_of_Item_3[3]), .out_6(Available_Stock_of_Item_3[2]),
    .out_7(Available_Stock_of_Item_3[1]), .out_8(Available_Stock_of_Item_3[0]));
  _4_Bit_Down_Counter u_4_bit_down_counter_4 (
    .Clock(and_6_out), .J__K(1'b1), .Preset(in_17), .Clear(Reset_Button),
    .out_5(Available_Stock_of_Item_4[3]), .out_6(Available_Stock_of_Item_4[2]),
    .out_7(Available_Stock_of_Item_4[1]), .out_8(Available_Stock_of_Item_4[0]));
  _4_Bit_Down_Counter u_4_bit_down_counter_5 (
    .Clock(and_7_out), .J__K(1'b1), .Preset(in_21), .Clear(Reset_Button),
    .out_5(Available_Stock_of_Item_5[3]), .out_6(Available_Stock_of_Item_5[2]),
    .out_7(Available_Stock_of_Item_5[1]), .out_8(Available_Stock_of_Item_5[0]));
  _4_Bit_Down_Counter u_4_bit_down_counter_6 (
    .Clock(and_8_out), .J__K(1'b1), .Preset(in_25), .Clear(Reset_Button),
    .out_5(Available_Stock_of_Item_6[3]), .out_6(Available_Stock_of_Item_6[2]),
    .out_7(Available_Stock_of_Item_6[1]), .out_8(Available_Stock_of_Item_6[0]));

  // Notes on the sheet:
  //   Starter Section
  //   Main Section
  //   Dessert Section
  //   7 Bit Up Counter
  //   Normal Service
  //   Priority Service
  //   4 Bit Down Counter
  //   4 Bit Down Counter
  //   4 Bit Down Counter
  //   4 Bit Down Counter
  //   4 Bit Down Counter
  //   4 Bit Down Counter
  //   PRIORITY DINE
  //   S2-T14
  //   Yashwanth R 231CS265
  //   Pranav Venkat YK 231CS242
  //   Mithun Patil V N 231CS234
  //   INSTRUCTIONS
  //   1. Switch on Ticks enabled option in Simulate Section.
  //   4. Click on the ready button when the order is ready.
  //   2. Double click the Reset button only first time to set all available stocks to 15(1111).
  //   3. Click on start Button and give the order and also select the priority and turn off the start button. 
endmodule

module Priority_service (
  input  Start_Button,
  input  _2_Bit_Up,
  input  in_3,
  input  in_4,
  input  in_5,
  input  in_6,
  input  in_7,
  input  Item_1,
  input  Ready_Button,
  input  Item_2,
  input  PriorityS,
  input  PrioriySL,
  input  in_13,
  input  in_14,
  input  Item_3,
  input  Item_4,
  input  in_17,
  input  Ready_Button_2,
  input  PriorityM,
  input  PriorityML,
  input  in_21,
  input  in_22,
  input  _5_by_2,
  input  in_24,
  input  in_25,
  input  Item_5,
  input  Item_6,
  input  in_28,
  input  Ready_Button_3,
  input  PriorityJ,
  input  PriorityJL,
  input  in_32,
  input  in_33,
  input  Priority_Service,
  input  in_35,
  output [4:0] Total_Estimated_Time_to_prepare,
  output [6:0] Total_Cost_of_the_items,
  output [3:0] Priority_Fee,
  output [3:0] Estimated_Time_to_preapre_in_each_section,
  output [5:0] Money_to_be_returned
);

  wire and_11_out, and_12_out, and_13_out, and_14_out, and_15_out, and_16_out, and_17_out, and_18_out,
       and_19_out, and_20_out, and_21_out, and_22_out, and_23_out, and_24_out, and_25_out, and_26_out,
       divide_by_2_1_b0, divide_by_2_1_b1, divide_by_2_1_b2, divide_by_2_1_b3, divide_by_2_1_b4,
       divide_by_2_1_b5, divide_by_10_1_b0, divide_by_10_1_b1, divide_by_10_1_b2, divide_by_10_1_b3,
       half_adder_1_carry, half_adder_1_sum, half_adder_2_carry, half_adder_2_sum, half_adder_3_carry,
       half_adder_3_sum, n2_bit_up_counter_1_out_4, n2_bit_up_counter_1_out_5, n3_by_2_multiplier_1_s0,
       n3_by_2_multiplier_1_s1, n3_by_2_multiplier_1_s2, n3_by_2_multiplier_1_s3, n3_by_2_multiplier_2_s0,
       n3_by_2_multiplier_2_s1, n3_by_2_multiplier_2_s2, n3_by_2_multiplier_2_s3, n3_by_2_multiplier_3_s0,
       n3_by_2_multiplier_3_s1, n3_by_2_multiplier_3_s2, n3_by_2_multiplier_3_s3, n4_bit_adder_1_carry,
       n4_bit_adder_1_s0, n4_bit_adder_1_s1, n4_bit_adder_1_s2, n4_bit_adder_1_s3, n4_bit_adder_2_carry,
       n5_bit_adder_1_carry, n5_bit_adder_1_s0, n5_bit_adder_1_s1, n5_bit_adder_1_s2, n5_bit_adder_1_s3,
       n5_bit_adder_1_s4, n5_bit_up_counter_1_lsb, n5_bit_up_counter_1_out_3, n5_bit_up_counter_1_out_4,
       n5_bit_up_counter_1_out_5, n5_bit_up_counter_1_out_6, n5_bit_up_counter_2_lsb,
       n5_bit_up_counter_2_out_3, n5_bit_up_counter_2_out_4, n5_bit_up_counter_2_out_5,
       n5_bit_up_counter_2_out_6, n5_bit_up_counter_3_lsb, n5_bit_up_counter_3_out_3,
       n5_bit_up_counter_3_out_4, n5_bit_up_counter_3_out_5, n5_bit_up_counter_3_out_6,
       n5_by_2_multiplier_1_s0, n5_by_2_multiplier_1_s1, n5_by_2_multiplier_1_s2, n5_by_2_multiplier_1_s3,
       n5_by_2_multiplier_1_s4, n5_by_2_multiplier_1_s5, n5_by_2_multiplier_2_s0, n5_by_2_multiplier_2_s1,
       n5_by_2_multiplier_2_s2, n5_by_2_multiplier_2_s3, n5_by_2_multiplier_2_s4, n5_by_2_multiplier_2_s5,
       n5_by_2_multiplier_3_s0, n5_by_2_multiplier_3_s1, n5_by_2_multiplier_3_s2, n5_by_2_multiplier_3_s3,
       n5_by_2_multiplier_3_s4, n5_by_2_multiplier_3_s5, n6_bit_adder_1_carry, n6_bit_adder_1_s0,
       n6_bit_adder_1_s1, n6_bit_adder_1_s2, n6_bit_adder_1_s3, n6_bit_adder_1_s4, n6_bit_adder_1_s5,
       n6_bit_adder_2_carry, n6_bit_adder_3_s0, n6_bit_adder_3_s1, n6_bit_adder_3_s2, n6_bit_adder_3_s3,
       n6_bit_adder_3_s4, n6_bit_adder_3_s5, n6_bit_comparator_1_a_b, not_1_out, not_2_out, not_3_out,
       or_3_out, subtract_by_1_1_out_6, subtract_by_1_1_out_7, subtract_by_1_1_out_8, subtract_by_1_2_out_6,
       subtract_by_1_2_out_7, subtract_by_1_2_out_8, subtract_by_1_3_out_6, subtract_by_1_3_out_7,
       subtract_by_1_3_out_8, two_bit_comparator_1_a_b, two_bit_comparator_2_a_b, two_bit_comparator_3_a_b;

  and and_1 (Priority_Fee[3], Priority_Service, divide_by_10_1_b3);
  and and_2 (Priority_Fee[2], Priority_Service, divide_by_10_1_b2);
  Half_Adder half_adder_1 (.A(Item_3), .B(Item_4), .Sum(half_adder_1_sum), .Carry(half_adder_1_carry));
  _5_by_2_Multiplier u_5_by_2_multiplier_1 (
    .B0(half_adder_2_sum), .B1(half_adder_2_carry), .A4(in_22), .A3(1'b1), .A2(_5_by_2), .A1(1'b1),
    .A0(in_24), .S5(n5_by_2_multiplier_1_s5), .S4(n5_by_2_multiplier_1_s4), .S3(n5_by_2_multiplier_1_s3),
    .S2(n5_by_2_multiplier_1_s2), .S1(n5_by_2_multiplier_1_s1), .S0(n5_by_2_multiplier_1_s0));
  Half_Adder half_adder_2 (.A(Item_5), .B(Item_6), .Sum(half_adder_2_sum), .Carry(half_adder_2_carry));
  Divide_by_10 divide_by_10_1 (
    .A6(Total_Cost_of_the_items[6]), .A5(Total_Cost_of_the_items[5]), .A4(Total_Cost_of_the_items[4]),
    .A3(Total_Cost_of_the_items[3]), .A2(Total_Cost_of_the_items[2]), .A1(Total_Cost_of_the_items[1]),
    .A0(Total_Cost_of_the_items[0]), .B0(divide_by_10_1_b0), .B1(divide_by_10_1_b1), .B2(divide_by_10_1_b2),
    .B3(divide_by_10_1_b3));
  and and_3 (Priority_Fee[1], divide_by_10_1_b1, Priority_Service);
  Half_Adder half_adder_3 (.A(Item_1), .B(Item_2), .Sum(half_adder_3_sum), .Carry(half_adder_3_carry));
  _5_by_2_Multiplier u_5_by_2_multiplier_2 (
    .B0(half_adder_1_sum), .B1(half_adder_1_carry), .A4(1'b1), .A3(1'b1), .A2(1'b1), .A1(1'b1), .A0(in_14),
    .S5(n5_by_2_multiplier_2_s5), .S4(n5_by_2_multiplier_2_s4), .S3(n5_by_2_multiplier_2_s3),
    .S2(n5_by_2_multiplier_2_s2), .S1(n5_by_2_multiplier_2_s1), .S0(n5_by_2_multiplier_2_s0));
  and and_4 (Priority_Fee[0], divide_by_10_1_b0, Priority_Service);
  _6_Bit_Adder u_6_bit_adder_1 (
    .B5(n5_by_2_multiplier_2_s5), .A5(n5_by_2_multiplier_3_s5), .B4(n5_by_2_multiplier_2_s4),
    .A4(n5_by_2_multiplier_3_s4), .B3(n5_by_2_multiplier_2_s3), .A3(n5_by_2_multiplier_3_s3),
    .B2(n5_by_2_multiplier_2_s2), .A2(n5_by_2_multiplier_3_s2), .B1(n5_by_2_multiplier_2_s1),
    .A1(n5_by_2_multiplier_3_s1), .B0(n5_by_2_multiplier_2_s0), .A0(n5_by_2_multiplier_3_s0),
    .Carry(n6_bit_adder_1_carry), .S5(n6_bit_adder_1_s5), .S4(n6_bit_adder_1_s4), .S3(n6_bit_adder_1_s3),
    .S2(n6_bit_adder_1_s2), .S1(n6_bit_adder_1_s1), .S0(n6_bit_adder_1_s0));
  _6_Bit_Adder u_6_bit_adder_2 (
    .B5(n5_by_2_multiplier_1_s5), .A5(n6_bit_adder_1_s5), .B4(n5_by_2_multiplier_1_s4),
    .A4(n6_bit_adder_1_s4), .B3(n5_by_2_multiplier_1_s3), .A3(n6_bit_adder_1_s3),
    .B2(n5_by_2_multiplier_1_s2), .A2(n6_bit_adder_1_s2), .B1(n5_by_2_multiplier_1_s1),
    .A1(n6_bit_adder_1_s1), .B0(n5_by_2_multiplier_1_s0), .A0(n6_bit_adder_1_s0),
    .Carry(n6_bit_adder_2_carry), .S5(Total_Cost_of_the_items[5]), .S4(Total_Cost_of_the_items[4]),
    .S3(Total_Cost_of_the_items[3]), .S2(Total_Cost_of_the_items[2]), .S1(Total_Cost_of_the_items[1]),
    .S0(Total_Cost_of_the_items[0]));
  or or_1 (Total_Cost_of_the_items[6], n6_bit_adder_1_carry, n6_bit_adder_2_carry);
  _5_by_2_Multiplier u_5_by_2_multiplier_3 (
    .B0(half_adder_3_sum), .B1(half_adder_3_carry), .A4(1'b1), .A3(in_4), .A2(1'b1), .A1(in_5), .A0(in_6),
    .S5(n5_by_2_multiplier_3_s5), .S4(n5_by_2_multiplier_3_s4), .S3(n5_by_2_multiplier_3_s3),
    .S2(n5_by_2_multiplier_3_s2), .S1(n5_by_2_multiplier_3_s1), .S0(n5_by_2_multiplier_3_s0));
  and and_5 (Money_to_be_returned[4], divide_by_2_1_b4, and_26_out);
  and and_6 (Money_to_be_returned[5], divide_by_2_1_b5, and_26_out);
  and and_7 (Money_to_be_returned[3], divide_by_2_1_b3, and_26_out);
  Subtract_by_1 subtract_by_1_1 (
    .in_4(Priority_Service), .in_5(in_7), .A2(1'b1), .A1(in_3), .A0(1'b1), .out_6(subtract_by_1_1_out_6),
    .out_7(subtract_by_1_1_out_7), .out_8(subtract_by_1_1_out_8));
  _3_by_2_Multiplier u_3_by_2_multiplier_1 (
    .B0(half_adder_3_sum), .B1(half_adder_3_carry), .A2(subtract_by_1_1_out_6), .A1(subtract_by_1_1_out_7),
    .A0(subtract_by_1_1_out_8), .S3(n3_by_2_multiplier_1_s3), .S2(n3_by_2_multiplier_1_s2),
    .S1(n3_by_2_multiplier_1_s1), .S0(n3_by_2_multiplier_1_s0));
  Subtract_by_1 subtract_by_1_2 (
    .in_4(Priority_Service), .in_5(in_17), .A2(1'b1), .A1(1'b1), .A0(1'b1), .out_6(subtract_by_1_2_out_6),
    .out_7(subtract_by_1_2_out_7), .out_8(subtract_by_1_2_out_8));
  _3_by_2_Multiplier u_3_by_2_multiplier_2 (
    .B0(half_adder_1_sum), .B1(half_adder_1_carry), .A2(subtract_by_1_2_out_6), .A1(subtract_by_1_2_out_7),
    .A0(subtract_by_1_2_out_8), .S3(n3_by_2_multiplier_2_s3), .S2(n3_by_2_multiplier_2_s2),
    .S1(n3_by_2_multiplier_2_s1), .S0(n3_by_2_multiplier_2_s0));
  Subtract_by_1 subtract_by_1_3 (
    .in_4(Priority_Service), .in_5(in_28), .A2(in_25), .A1(1'b1), .A0(1'b1), .out_6(subtract_by_1_3_out_6),
    .out_7(subtract_by_1_3_out_7), .out_8(subtract_by_1_3_out_8));
  _3_by_2_Multiplier u_3_by_2_multiplier_3 (
    .B0(half_adder_2_sum), .B1(half_adder_2_carry), .A2(subtract_by_1_3_out_6), .A1(subtract_by_1_3_out_7),
    .A0(subtract_by_1_3_out_8), .S3(n3_by_2_multiplier_3_s3), .S2(n3_by_2_multiplier_3_s2),
    .S1(n3_by_2_multiplier_3_s1), .S0(n3_by_2_multiplier_3_s0));
  Divide_by_2 divide_by_2_1 (
    .A6(Total_Cost_of_the_items[6]), .A5(Total_Cost_of_the_items[5]), .A4(Total_Cost_of_the_items[4]),
    .A3(Total_Cost_of_the_items[3]), .A2(Total_Cost_of_the_items[2]), .A1(Total_Cost_of_the_items[1]),
    .A0(Total_Cost_of_the_items[0]), .B0(divide_by_2_1_b0), .B1(divide_by_2_1_b1), .B2(divide_by_2_1_b2),
    .B3(divide_by_2_1_b3), .B4(divide_by_2_1_b4), .B5(divide_by_2_1_b5));
  and and_8 (Money_to_be_returned[2], divide_by_2_1_b2, and_26_out);
  and and_9 (Money_to_be_returned[0], divide_by_2_1_b0, and_26_out);
  and and_10 (Money_to_be_returned[1], divide_by_2_1_b1, and_26_out);
  _4_Bit_Adder u_4_bit_adder_1 (
    .B3(n3_by_2_multiplier_2_s3), .A3(n3_by_2_multiplier_1_s3), .B2(n3_by_2_multiplier_2_s2),
    .A2(n3_by_2_multiplier_1_s2), .B1(n3_by_2_multiplier_2_s1), .A1(n3_by_2_multiplier_1_s1),
    .B0(n3_by_2_multiplier_2_s0), .A0(n3_by_2_multiplier_1_s0), .Carry(n4_bit_adder_1_carry),
    .S3(n4_bit_adder_1_s3), .S2(n4_bit_adder_1_s2), .S1(n4_bit_adder_1_s1), .S0(n4_bit_adder_1_s0));
  _4_Bit_Adder u_4_bit_adder_2 (
    .B3(n4_bit_adder_1_s3), .A3(n3_by_2_multiplier_3_s3), .B2(n4_bit_adder_1_s2),
    .A2(n3_by_2_multiplier_3_s2), .B1(n4_bit_adder_1_s1), .A1(n3_by_2_multiplier_3_s1),
    .B0(n4_bit_adder_1_s0), .A0(n3_by_2_multiplier_3_s0), .Carry(n4_bit_adder_2_carry),
    .S3(Total_Estimated_Time_to_prepare[3]), .S2(Total_Estimated_Time_to_prepare[2]),
    .S1(Total_Estimated_Time_to_prepare[1]), .S0(Total_Estimated_Time_to_prepare[0]));
  or or_2 (Total_Estimated_Time_to_prepare[4], n4_bit_adder_1_carry, n4_bit_adder_2_carry);
  _2_bit_Up_Counter u_2_bit_up_counter_1 (
    .Clock(or_3_out), .J__K(1'b1), .Preset__Clear(_2_Bit_Up), .out_4(n2_bit_up_counter_1_out_4),
    .out_5(n2_bit_up_counter_1_out_5));
  Two_Bit_Comparator two_bit_comparator_1 (
    .B0(PriorityS), .A0(n2_bit_up_counter_1_out_4), .B1(PrioriySL), .A1(n2_bit_up_counter_1_out_5),
    .A_B(two_bit_comparator_1_a_b));  // open: A_B_2, A_B_3
  and and_11 (and_11_out, n3_by_2_multiplier_1_s3, two_bit_comparator_1_a_b);
  Two_Bit_Comparator two_bit_comparator_2 (
    .B0(PriorityM), .A0(n2_bit_up_counter_1_out_4), .B1(PriorityML), .A1(n2_bit_up_counter_1_out_5),
    .A_B(two_bit_comparator_2_a_b));  // open: A_B_2, A_B_3
  and and_12 (and_12_out, n3_by_2_multiplier_2_s3, two_bit_comparator_2_a_b);
  Two_Bit_Comparator two_bit_comparator_3 (
    .B0(PriorityJ), .A0(n2_bit_up_counter_1_out_4), .B1(PriorityJL), .A1(n2_bit_up_counter_1_out_5),
    .A_B(two_bit_comparator_3_a_b));  // open: A_B_2, A_B_3
  and and_13 (and_13_out, n3_by_2_multiplier_3_s3, two_bit_comparator_3_a_b);
  or or_3 (or_3_out, Start_Button, Ready_Button_3, Ready_Button, Ready_Button_2);
  and and_14 (and_14_out, n3_by_2_multiplier_1_s2, two_bit_comparator_1_a_b);
  and and_15 (and_15_out, n3_by_2_multiplier_2_s2, two_bit_comparator_2_a_b);
  and and_16 (and_16_out, n3_by_2_multiplier_3_s2, two_bit_comparator_3_a_b);
  and and_17 (and_17_out, n3_by_2_multiplier_1_s1, two_bit_comparator_1_a_b);
  and and_18 (and_18_out, n3_by_2_multiplier_1_s0, two_bit_comparator_1_a_b);
  and and_19 (and_19_out, n3_by_2_multiplier_2_s1, two_bit_comparator_2_a_b);
  and and_20 (and_20_out, n3_by_2_multiplier_2_s0, two_bit_comparator_2_a_b);
  and and_21 (and_21_out, n3_by_2_multiplier_3_s1, two_bit_comparator_3_a_b);
  and and_22 (and_22_out, n3_by_2_multiplier_3_s0, two_bit_comparator_3_a_b);
  not not_1 (not_1_out, Ready_Button_2);
  not not_2 (not_2_out, Ready_Button_3);
  or or_4 (Estimated_Time_to_preapre_in_each_section[3], and_13_out, and_12_out, and_11_out);
  not not_3 (not_3_out, Ready_Button);
  and and_23 (and_23_out, not_1_out, two_bit_comparator_2_a_b);
  and and_24 (and_24_out, not_2_out, two_bit_comparator_3_a_b);
  or or_5 (Estimated_Time_to_preapre_in_each_section[2], and_16_out, and_15_out, and_14_out);
  and and_25 (and_25_out, not_3_out, two_bit_comparator_1_a_b);
  _5_Bit_Up_Counter u_5_bit_up_counter_1 (
    .J__K(and_25_out), .Preset__Clear(in_13), .out_3(n5_bit_up_counter_1_out_3),
    .out_4(n5_bit_up_counter_1_out_4), .out_5(n5_bit_up_counter_1_out_5), .out_6(n5_bit_up_counter_1_out_6),
    .LSB(n5_bit_up_counter_1_lsb));
  _5_Bit_Up_Counter u_5_bit_up_counter_2 (
    .J__K(and_23_out), .Preset__Clear(in_21), .out_3(n5_bit_up_counter_2_out_3),
    .out_4(n5_bit_up_counter_2_out_4), .out_5(n5_bit_up_counter_2_out_5), .out_6(n5_bit_up_counter_2_out_6),
    .LSB(n5_bit_up_counter_2_lsb));
  _5_Bit_Up_Counter u_5_bit_up_counter_3 (
    .J__K(and_24_out), .Preset__Clear(in_32), .out_3(n5_bit_up_counter_3_out_3),
    .out_4(n5_bit_up_counter_3_out_4), .out_5(n5_bit_up_counter_3_out_5), .out_6(n5_bit_up_counter_3_out_6),
    .LSB(n5_bit_up_counter_3_lsb));
  or or_6 (Estimated_Time_to_preapre_in_each_section[1], and_21_out, and_19_out, and_17_out);
  or or_7 (Estimated_Time_to_preapre_in_each_section[0], and_22_out, and_20_out, and_18_out);
  and and_26 (and_26_out, Priority_Service, n6_bit_comparator_1_a_b);
  _6_Bit_Comparator u_6_bit_comparator_1 (
    .B5(in_35), .A5(n6_bit_adder_3_s5), .B4(Total_Estimated_Time_to_prepare[4]), .A4(n6_bit_adder_3_s4),
    .B3(Total_Estimated_Time_to_prepare[3]), .A3(n6_bit_adder_3_s3), .B2(Total_Estimated_Time_to_prepare[2]),
    .A2(n6_bit_adder_3_s2), .B1(Total_Estimated_Time_to_prepare[1]), .A1(n6_bit_adder_3_s1),
    .B0(Total_Estimated_Time_to_prepare[0]), .A0(n6_bit_adder_3_s0), .A_B(n6_bit_comparator_1_a_b));
  _6_Bit_Adder u_6_bit_adder_3 (
    .B5(in_33), .A5(n5_bit_adder_1_carry), .B4(n5_bit_up_counter_3_out_3), .A4(n5_bit_adder_1_s4),
    .B3(n5_bit_up_counter_3_out_4), .A3(n5_bit_adder_1_s3), .B2(n5_bit_up_counter_3_out_5),
    .A2(n5_bit_adder_1_s2), .B1(n5_bit_up_counter_3_out_6), .A1(n5_bit_adder_1_s1),
    .B0(n5_bit_up_counter_3_lsb), .A0(n5_bit_adder_1_s0), .S5(n6_bit_adder_3_s5), .S4(n6_bit_adder_3_s4),
    .S3(n6_bit_adder_3_s3), .S2(n6_bit_adder_3_s2), .S1(n6_bit_adder_3_s1), .S0(n6_bit_adder_3_s0));  // open: Carry
  _5_Bit_Adder u_5_bit_adder_1 (
    .B4(n5_bit_up_counter_2_out_3), .A4(n5_bit_up_counter_1_out_3), .B3(n5_bit_up_counter_2_out_4),
    .A3(n5_bit_up_counter_1_out_4), .B2(n5_bit_up_counter_2_out_5), .A2(n5_bit_up_counter_1_out_5),
    .B1(n5_bit_up_counter_2_out_6), .A1(n5_bit_up_counter_1_out_6), .B0(n5_bit_up_counter_2_lsb),
    .A0(n5_bit_up_counter_1_lsb), .Carry(n5_bit_adder_1_carry), .S4(n5_bit_adder_1_s4),
    .S3(n5_bit_adder_1_s3), .S2(n5_bit_adder_1_s2), .S1(n5_bit_adder_1_s1), .S0(n5_bit_adder_1_s0));

  // Notes on the sheet:
  //   Starter Section
  //   Main Section
  //   Dessert Section
  //   Half Adder
  //   Half Adder
  //   Cost of each item
  //   Divide by 10
  //   Half Adder
  //   Cost of each item
  //   5 by 2 
  //   Multiplier
  //   Multiplier
  //   6 Bit Adder
  //   6 Bit Adder
  //   Cost of each item
  //   5 by 2 
  //   Multiplier
  //   Estimated Time of each item
  //   Estimated Time of each item
  //   Estimated Time of each item
  //   Divide by 2
  //   Subtract by 1
  //   3 by 2 Multiplier
  //   Subtract by 1
  //   3 by 2 Multiplier
  //   Subtract by 1
  //   3 by 2 Multiplier
  //   4 Bit Adder
  //   4 Bit Adder
  //   Counter
  //   2 Bit Comparator
  //   2 Bit Comparator
  //   2 Bit Comparator
  //   5 Bit Up Counter
  //   5 Bit Up Counter
  //   5 Bit Up Counter
  //   6 Bit Comparator
  //   Total time taken to serve
  //   5 Bit Adder
  //   6 Bit Adder
  //   Comparing Estimated time with Total time
endmodule
